// Digital circuit FSM_4.dig as structural Verilog
module FSM_4 (
  input  Clock,
  input  nexten_0,
  input  nexten_1,
  input  nexten_2,
  input  nexten_3,
  input  direct_statusen,
  input  [1:0] direct_status,
  input  [3:0] falling_edge_status,
  output [1:0] Status_cur
);

  wire and_5_out, bitselector_1_out, CUR0, CUR1, CUR2, CUR3, S0, S1, S2, S3, xor_1_out;
  wire [1:0] multiplexer_1_out, next;

  Decoder #(.Selector_Bits(2)) decoder_1 (.sel(Status_cur), .out_0(CUR0), .out_1(CUR1), .out_2(CUR2), .out_3(CUR3));
  and and_1 (S0, nexten_0, CUR0);
  and and_2 (S1, nexten_1, CUR1);
  and and_3 (S2, nexten_2, CUR2);
  and and_4 (S3, nexten_3, CUR3);
  assign next = S0 ? 2'b01 : 2'bz;  // Driver driver_1
  assign next = S1 ? 2'b10 : 2'bz;  // Driver driver_2
  assign next = S2 ? 2'b11 : 2'bz;  // Driver driver_3
  assign next = S3 ? 2'b00 : 2'bz;  // Driver driver_4
  and and_5 (and_5_out, ~S0, ~S1, ~S3, ~S2);  // And
  assign next = and_5_out ? Status_cur : 2'bz;  // Driver driver_5
  PullDown #(.Bits(2)) pulldown_1 (.out(next));
  Multiplexer #(.Bits(2)) multiplexer_1 (
    .sel(direct_statusen), .in_0(next), .in_1(direct_status), .out(multiplexer_1_out));
  PullDown pulldown_2 (.out(direct_statusen));
  BitSelector #(.Selector_Bits(2)) bitselector_1 (.in(falling_edge_status), .sel(Status_cur), .out(bitselector_1_out));
  PullDown #(.Bits(2)) pulldown_3 (.out(multiplexer_1_out));
  xor xor_1 (xor_1_out, Clock, bitselector_1_out);
  D_FF #(.Bits(2)) d_ff_1 (.D(multiplexer_1_out), .C(xor_1_out), .Q(Status_cur));  // open: nQ
  PullDown #(.Bits(2)) pulldown_4 (.out(Status_cur));

  // Other names for the same wires on the sheet: cur[1:0] = Status_cur

  // Notes on the sheet:
  //   Clock: Hz: 2
endmodule
