// Digital circuit PLIC.dig as structural Verilog
module PLIC (
  input  WE,
  input  [31:0] perint_code,
  input  [31:0] Addr_w,
  input  [31:0] Addr_r1,
  input  [31:0] Data_in,
  input  [31:0] mip_in,
  input  mret,
  input  TimerClock,
  input  Clock,
  output mip_seten,
  output [31:0] mip_set,
  output Out_en,
  output [31:0] Out_ra,
  output int_timer,
  output gate_peripheral,
  output [63:0] mtimcmp,
  output [63:0] mtime
);

  wire addr_compare_1_eq_out, addr_compare_2_eq_out, addr_compare_3_eq_out, addr_compare_4_eq_out,
       addr_compare_5_eq_out, addr_compare_6_eq_out, addr_compare_7_eq_out, and_1_out, and_2_out, and_3_out,
       and_4_out, and_7_out, comparator_1_gt, comparator_2_eq, comparator_3_eq, comparator_3_gt,
       comparator_3_lt, en_periph, or_1_out, or_3_out, we_mtc;
  wire [31:0] and_5_out, and_8_out, int_c, or_2_out, or_4_out, register_1_q;
  wire [63:0] mc_in, mtime_in;

  PullDown #(.Bits(32)) pulldown_1 (.out(perint_code));
  Comparator #(.Bits(32)) comparator_1 (.a(perint_code), .b({32{1'b0}}), .gt(comparator_1_gt));  // open: eq, lt
  Add #(.Bits(64)) add_1 (.a(mtime), .b(64'ha), .c_i(TimerClock), .s(mtime_in));  // open: c_o
  assign int_c = ~mret ? perint_code : 32'bz;  // DriverInvSel driverinvsel_1
  assign int_c = mret ? {32{1'b0}} : 32'bz;  // Driver driver_1
  or or_1 (or_1_out, mret, comparator_1_gt);
  Register #(.Bits(32)) register_1 (.D(int_c), .C(Clock), .en(or_1_out), .Q(register_1_q));
  Register #(.Bits(64)) u_mtime (.D(mtime_in), .C(TimerClock), .en(1'b1), .Q(mtime));
  addr_compare addr_compare_1 (.Addr_in1(Addr_w), .Addr_in2(32'hb0000000), .Eq_out(addr_compare_1_eq_out));
  addr_compare addr_compare_2 (.Addr_in1(Addr_w), .Addr_in2(32'hb0000004), .Eq_out(addr_compare_2_eq_out));
  addr_compare addr_compare_3 (.Addr_in1(Addr_r1), .Addr_in2(32'hb0000008), .Eq_out(addr_compare_3_eq_out));
  addr_compare addr_compare_4 (.Addr_in1(Addr_r1), .Addr_in2(32'hb0001000), .Eq_out(addr_compare_4_eq_out));
  and and_1 (and_1_out, WE, addr_compare_1_eq_out);
  assign mc_in = addr_compare_1_eq_out ? {mtimcmp[63:32], Data_in} : 64'bz;  // Driver driver_2
  and and_2 (and_2_out, WE, addr_compare_2_eq_out);
  assign mc_in = addr_compare_2_eq_out ? {Data_in, mtimcmp[31:0]} : 64'bz;  // Driver driver_3
  assign Out_ra = addr_compare_3_eq_out ? mtime[31:0] : 32'bz;  // Driver driver_4
  assign Out_ra = addr_compare_4_eq_out ? register_1_q : 32'bz;  // Driver driver_5
  Register #(.Bits(64)) mtimecmp (.D(mc_in), .C(Clock), .en(we_mtc), .Q(mtimcmp));
  PullDown pulldown_2 (.out(we_mtc));
  assign we_mtc = and_1_out ? 1'b1 : 1'bz;  // Driver driver_6
  assign we_mtc = and_2_out ? 1'b1 : 1'bz;  // Driver driver_7
  assign Out_en = addr_compare_3_eq_out ? 1'b1 : 1'bz;  // Driver driver_8
  assign Out_en = addr_compare_4_eq_out ? 1'b1 : 1'bz;  // Driver driver_9
  addr_compare addr_compare_5 (.Addr_in1(Addr_r1), .Addr_in2(32'hb000000c), .Eq_out(addr_compare_5_eq_out));
  Comparator #(.Bits(32)) comparator_2 (
    .a(perint_code), .b({32{1'b0}}), .gt(en_periph), .eq(comparator_2_eq));  // open: lt
  addr_compare addr_compare_6 (.Addr_in1(Addr_r1), .Addr_in2(32'hb0000000), .Eq_out(addr_compare_6_eq_out));
  addr_compare addr_compare_7 (.Addr_in1(Addr_r1), .Addr_in2(32'hb0000004), .Eq_out(addr_compare_7_eq_out));
  and and_3 (and_3_out, ~mip_in[11], en_periph);  // And
  and and_4 (and_4_out, comparator_2_eq, mip_in[11]);
  assign Out_ra = addr_compare_5_eq_out ? mtime[63:32] : 32'bz;  // Driver driver_10
  assign and_5_out = mip_in & 32'h1001;  // And and_5, 32 bits wide
  assign Out_ra = addr_compare_6_eq_out ? mtimcmp[31:0] : 32'bz;  // Driver driver_11
  assign Out_ra = addr_compare_7_eq_out ? mtimcmp[63:32] : 32'bz;  // Driver driver_12
  assign Out_en = addr_compare_5_eq_out ? 1'b1 : 1'bz;  // Driver driver_13
  assign mip_set = and_4_out ? and_5_out : 32'bz;  // Driver driver_14
  assign Out_en = addr_compare_6_eq_out ? 1'b1 : 1'bz;  // Driver driver_15
  assign Out_en = addr_compare_7_eq_out ? 1'b1 : 1'bz;  // Driver driver_16
  assign or_2_out = 32'h800 | mip_in;  // Or or_2, 32 bits wide
  Comparator #(.Bits(64)) comparator_3 (
    .a(mtimcmp), .b(mtime), .gt(comparator_3_gt), .eq(comparator_3_eq), .lt(comparator_3_lt));
  assign mip_set = and_3_out ? or_2_out : 32'bz;  // Driver driver_17
  assign mip_seten = and_4_out ? 1'b1 : 1'bz;  // Driver driver_18
  or or_3 (or_3_out, comparator_3_gt, comparator_3_eq);
  and and_6 (int_timer, comparator_3_lt, ~mip_in[7]);  // And
  assign mip_seten = and_3_out ? 1'b1 : 1'bz;  // Driver driver_19
  and and_7 (and_7_out, or_3_out, mip_in[7]);
  PullDown pulldown_3 (.out(Out_en));
  assign and_8_out = 32'h101 & mip_in;  // And and_8, 32 bits wide
  assign or_4_out = 32'h80 | mip_in;  // Or or_4, 32 bits wide
  PullDown pulldown_4 (.out(mip_seten));
  assign mip_set = and_7_out ? and_8_out : 32'bz;  // Driver driver_20
  assign mip_set = int_timer ? or_4_out : 32'bz;  // Driver driver_21
  assign mip_seten = and_7_out ? 1'b1 : 1'bz;  // Driver driver_22
  assign mip_seten = int_timer ? 1'b1 : 1'bz;  // Driver driver_23

  assign gate_peripheral = mip_in[11];

  // Other names for the same wires on the sheet: C = Clock; cur_perint_code[31:0] = perint_code;
  //   mc_out[63:0] = mtimcmp; mip_soft = mip_in[3]; mip_timer = mip_in[7]; mip_peripheral = mip_in[11];
  //   mip_out[31:0] = mip_set; mtime_out[63:0] = mtime; TC = TimerClock; timer_int = int_timer

  // Notes on the sheet:
  //   TimerClock: Hz: 100
endmodule
