// Digital circuit addr2reg_num.dig as structural Verilog
module addr2reg_num (
  input  [31:0] Addr,
  input  [31:0] Addr_base,
  input  EN,
  input  [2:0] num,
  output [2:0] REG_num,
  output OE,
  output [7:0] one_hot
);

  wire comparator_1_eq, comparator_2_eq, comparator_3_eq, comparator_4_eq, comparator_4_lt, or_1_out,
       sub_1_c_o;
  wire [7:0] bitextender_1_out, decoder_1_out_0, div_1_r;
  wire [7:3] div_1_q;
  wire [31:0] sub_1_s;

  Sub #(.Bits(32)) sub_1 (.a(Addr), .b(Addr_base), .c_i(1'b0), .s(sub_1_s), .c_o(sub_1_c_o));
  Comparator #(.Bits(24)) comparator_1 (.a(sub_1_s[31:8]), .b({24{1'b0}}), .eq(comparator_1_eq));  // open: gt, lt
  Div #(.Bits(8)) div_1 (.a(sub_1_s[7:0]), .b(8'h4), .q({div_1_q, REG_num}), .r(div_1_r));
  Comparator #(.Bits(8)) comparator_2 (.a(div_1_r), .b({8{1'b0}}), .eq(comparator_2_eq));  // open: gt, lt
  Comparator #(.Bits(5)) comparator_3 (.a(div_1_q), .b({5{1'b0}}), .eq(comparator_3_eq));  // open: gt, lt
  Comparator #(.Bits(3)) comparator_4 (.a(REG_num), .b(num), .eq(comparator_4_eq), .lt(comparator_4_lt));  // open: gt
  or or_1 (or_1_out, comparator_4_eq, comparator_4_lt);
  Decoder #(.Selector_Bits(3)) decoder_1 (
    .sel(REG_num), .out_0(decoder_1_out_0[0]), .out_1(decoder_1_out_0[1]), .out_2(decoder_1_out_0[2]),
    .out_3(decoder_1_out_0[3]), .out_4(decoder_1_out_0[4]), .out_5(decoder_1_out_0[5]),
    .out_6(decoder_1_out_0[6]), .out_7(decoder_1_out_0[7]));
  and and_1 (OE, or_1_out, comparator_3_eq, comparator_2_eq, comparator_1_eq, ~sub_1_c_o, EN);  // And
  BitExtender #(.inputBits(1), .outputBits(8)) bitextender_1 (.in(OE), .out(bitextender_1_out));
  assign one_hot = decoder_1_out_0 & bitextender_1_out;  // And and_2, 8 bits wide

  // Notes on the sheet:
  //   num: How many number of 32bit-registers have been defined.
endmodule
