// Digital circuit alu.dig as structural Verilog
module alu (
  input  [18:0] Alu_in,
  input  [31:0] rs1_in,
  input  [31:0] rs2_in,
  input  [11:0] Imm12_in,
  output EN_out,
  output [31:0] rd_out,
  output [31:0] InvalidOP_out
);

  wire comparator_1_lt, comparator_2_lt, comparator_3_lt, comparator_4_lt, multiplexer_1_out, or_1_out;
  wire [4:0] priorityencoder_1_num;
  wire [5:0] driverinvsel_1_out;
  wire [31:0] add_1_s, add_2_s, and_1_out, and_2_out, barrelshifter_1_out, barrelshifter_2_out,
       barrelshifter_3_out, barrelshifter_4_out, barrelshifter_5_out, barrelshifter_6_out, bitextender_1_out,
       bitextender_2_out, bitextender_3_out, bitextender_4_out, bitextender_5_out, bitextender_6_out,
       bitextender_7_out, bitextender_8_out, bitextender_9_out, or_2_out, or_3_out, sub_1_s, xor_1_out,
       xor_2_out;

  or or_1 (or_1_out, Alu_in[16], Alu_in[11], Alu_in[15]);
  Multiplexer multiplexer_1 (.sel(or_1_out), .in_0(1'b0), .in_1(Imm12_in[5]), .out(multiplexer_1_out));
  assign InvalidOP_out = multiplexer_1_out ? 32'h2 : 32'bz;  // Driver driver_1
  PriorityEncoder #(.Selector_Bits(5)) priorityencoder_1 (
    .in0(Alu_in[0]), .in1(Alu_in[1]), .in2(Alu_in[2]), .in3(Alu_in[3]), .in4(Alu_in[4]), .in5(Alu_in[5]),
    .in6(Alu_in[6]), .in7(Alu_in[7]), .in8(Alu_in[8]), .in9(Alu_in[9]), .in10(Alu_in[10]), .in11(Alu_in[11]),
    .in12(Alu_in[12]), .in13(Alu_in[13]), .in14(Alu_in[14]), .in15(Alu_in[15]), .in16(Alu_in[16]),
    .in17(Alu_in[17]), .in18(Alu_in[18]), .in19(1'b0), .in20(1'b0), .in21(1'b0), .in22(1'b0), .in23(1'b0),
    .in24(1'b0), .in25(1'b0), .in26(1'b0), .in27(1'b0), .in28(1'b0), .in29(1'b0), .in30(1'b0), .in31(1'b0),
    .num(priorityencoder_1_num), .any(EN_out));
  BitExtender #(.inputBits(12), .outputBits(32)) bitextender_1 (.in(Imm12_in), .out(bitextender_1_out));
  BitExtender #(.inputBits(12), .outputBits(32)) bitextender_2 (.in(Imm12_in), .out(bitextender_2_out));
  BitExtender #(.inputBits(12), .outputBits(32)) bitextender_3 (.in(Imm12_in), .out(bitextender_3_out));
  assign xor_1_out = rs1_in ^ rs2_in;  // XOr xor_1, 32 bits wide
  assign or_2_out = rs1_in | rs2_in;  // Or or_2, 32 bits wide
  assign and_1_out = rs1_in & rs2_in;  // And and_1, 32 bits wide
  assign xor_2_out = rs1_in ^ bitextender_1_out;  // XOr xor_2, 32 bits wide
  assign or_3_out = rs1_in | bitextender_2_out;  // Or or_3, 32 bits wide
  assign and_2_out = rs1_in & bitextender_3_out;  // And and_2, 32 bits wide
  BitExtender #(.inputBits(12), .outputBits(32)) bitextender_4 (.in(Imm12_in), .out(bitextender_4_out));
  assign driverinvsel_1_out = ~Imm12_in[5] ? {1'b0, Imm12_in[4:0]} : 6'bz;  // DriverInvSel driverinvsel_1
  BitExtender #(.inputBits(12), .outputBits(32)) bitextender_5 (.in(Imm12_in), .out(bitextender_5_out));
  Add #(.Bits(32)) add_1 (.a(rs1_in), .b(rs2_in), .c_i(1'b0), .s(add_1_s));  // open: c_o
  Sub #(.Bits(32)) sub_1 (.a(rs1_in), .b(rs2_in), .c_i(1'b0), .s(sub_1_s));  // open: c_o
  BarrelShifter #(.Bits(32)) barrelshifter_1 (.in(rs1_in), .shift({1'b0, rs2_in[4:0]}), .out(barrelshifter_1_out));
  Comparator #(.Signed("true"), .Bits(32)) comparator_1 (.a(rs1_in), .b(rs2_in), .lt(comparator_1_lt));  // open: gt, eq
  Comparator #(.Bits(32)) comparator_2 (.a(rs1_in), .b(rs2_in), .lt(comparator_2_lt));  // open: gt, eq
  BarrelShifter #(.Bits(32), .barrelShifterMode("arithmetic"), .direction("right")) barrelshifter_2 (
    .in(rs1_in), .shift({1'b0, rs2_in[4:0]}), .out(barrelshifter_2_out));
  BarrelShifter #(.Bits(32), .direction("right")) barrelshifter_3 (
    .in(rs1_in), .shift({1'b0, rs2_in[4:0]}), .out(barrelshifter_3_out));
  Add #(.Bits(32)) add_2 (.a(rs1_in), .b(bitextender_4_out), .c_i(1'b0), .s(add_2_s));  // open: c_o
  BarrelShifter #(.Bits(32)) barrelshifter_4 (.in(rs1_in), .shift(driverinvsel_1_out), .out(barrelshifter_4_out));
  BarrelShifter #(.Bits(32), .barrelShifterMode("arithmetic"), .direction("right")) barrelshifter_5 (
    .in(rs1_in), .shift(driverinvsel_1_out), .out(barrelshifter_5_out));
  BarrelShifter #(.Bits(32), .direction("right")) barrelshifter_6 (
    .in(rs1_in), .shift(driverinvsel_1_out), .out(barrelshifter_6_out));
  Comparator #(.Signed("true"), .Bits(32)) comparator_3 (
    .a(rs1_in), .b(bitextender_5_out), .lt(comparator_3_lt));  // open: gt, eq
  Comparator #(.Bits(32)) comparator_4 (.a(rs1_in), .b({{20{1'b0}}, Imm12_in}), .lt(comparator_4_lt));  // open: gt, eq
  BitExtender #(.inputBits(1), .outputBits(32)) bitextender_6 (.in(comparator_1_lt), .out(bitextender_6_out));
  BitExtender #(.inputBits(1), .outputBits(32)) bitextender_7 (.in(comparator_2_lt), .out(bitextender_7_out));
  BitExtender #(.inputBits(1), .outputBits(32)) bitextender_8 (.in(comparator_3_lt), .out(bitextender_8_out));
  BitExtender #(.inputBits(1), .outputBits(32)) bitextender_9 (.in(comparator_4_lt), .out(bitextender_9_out));
  Multiplexer #(.Selector_Bits(5), .Bits(32)) multiplexer_2 (
    .sel(priorityencoder_1_num), .in_0(add_1_s), .in_1(sub_1_s), .in_2(barrelshifter_1_out),
    .in_3(bitextender_6_out), .in_4(bitextender_7_out), .in_5(xor_1_out), .in_6(barrelshifter_2_out),
    .in_7(barrelshifter_3_out), .in_8(or_2_out), .in_9(and_1_out), .in_10(add_2_s),
    .in_11(barrelshifter_4_out), .in_12(bitextender_8_out), .in_13(bitextender_9_out), .in_14(xor_2_out),
    .in_15(barrelshifter_6_out), .in_16(barrelshifter_5_out), .in_17(or_3_out), .in_18(and_2_out),
    .in_19({32{1'b0}}), .in_20({32{1'b0}}), .in_21({32{1'b0}}), .in_22({32{1'b0}}), .in_23({32{1'b0}}),
    .in_24({32{1'b0}}), .in_25({32{1'b0}}), .in_26({32{1'b0}}), .in_27({32{1'b0}}), .in_28({32{1'b0}}),
    .in_29({32{1'b0}}), .in_30({32{1'b0}}), .in_31({32{1'b0}}), .out(rd_out));

  // Other names for the same wires on the sheet: add = Alu_in[0]; sub = Alu_in[1]; sll = Alu_in[2]; slt = Alu_in[3];
  //   sltu = Alu_in[4]; xor = Alu_in[5]; sra = Alu_in[6]; srl = Alu_in[7]; or = Alu_in[8]; and = Alu_in[9];
  //   addi = Alu_in[10]; slli = Alu_in[11]; slti = Alu_in[12]; sltiu = Alu_in[13]; xori = Alu_in[14];
  //   srli = Alu_in[15]; srai = Alu_in[16]; ori = Alu_in[17]; andi = Alu_in[18]; rs1[31:0] = rs1_in;
  //   rs2[31:0] = rs2_in
endmodule
