// Digital circuit barrel_shifter1.dig as structural Verilog
module barrel_shifter1 (
  input  [1:0] shift,
  input  [3:0] in4,
  input  Direction,
  input  [1:0] mode,
  output [3:0] out4
);

  wire [3:0] out_ari_left, out_ari_right, out_logic_right, out_rotate_left, out_rotate_right;

  Multiplexer #(.Selector_Bits(3), .Bits(4)) multiplexer_1 (
    .sel({mode, Direction}), .in_0(out_rotate_left), .in_1(out_rotate_right), .in_2(out_ari_left),
    .in_3(out_logic_right), .in_4(out_ari_left), .in_5(out_ari_right), .in_6(4'b0000), .in_7(4'b0000),
    .out(out4));
  Multiplexer #(.Selector_Bits(2)) multiplexer_2 (
    .sel(shift), .in_0(in4[0]), .in_1(in4[3]), .in_2(in4[2]), .in_3(in4[1]), .out(out_rotate_left[0]));
  Multiplexer #(.Selector_Bits(2)) multiplexer_3 (
    .sel(shift), .in_0(in4[1]), .in_1(in4[0]), .in_2(in4[3]), .in_3(in4[2]), .out(out_rotate_left[1]));
  Multiplexer #(.Selector_Bits(2)) multiplexer_4 (
    .sel(shift), .in_0(in4[2]), .in_1(in4[1]), .in_2(in4[0]), .in_3(in4[3]), .out(out_rotate_left[2]));
  Multiplexer #(.Selector_Bits(2)) multiplexer_5 (
    .sel(shift), .in_0(in4[3]), .in_1(in4[2]), .in_2(in4[1]), .in_3(in4[0]), .out(out_rotate_left[3]));
  Multiplexer #(.Selector_Bits(2)) multiplexer_6 (
    .sel(shift), .in_0(in4[0]), .in_1(in4[1]), .in_2(in4[2]), .in_3(in4[3]), .out(out_rotate_right[0]));
  Multiplexer #(.Selector_Bits(2)) multiplexer_7 (
    .sel(shift), .in_0(in4[1]), .in_1(in4[2]), .in_2(in4[3]), .in_3(in4[0]), .out(out_rotate_right[1]));
  Multiplexer #(.Selector_Bits(2)) multiplexer_8 (
    .sel(shift), .in_0(in4[2]), .in_1(in4[3]), .in_2(in4[0]), .in_3(in4[1]), .out(out_rotate_right[2]));
  Multiplexer #(.Selector_Bits(2)) multiplexer_9 (
    .sel(shift), .in_0(in4[3]), .in_1(in4[0]), .in_2(in4[1]), .in_3(in4[2]), .out(out_rotate_right[3]));
  Multiplexer #(.Selector_Bits(2)) multiplexer_10 (
    .sel(shift), .in_0(in4[0]), .in_1(1'b0), .in_2(1'b0), .in_3(1'b0), .out(out_ari_left[0]));
  Multiplexer #(.Selector_Bits(2)) multiplexer_11 (
    .sel(shift), .in_0(in4[1]), .in_1(in4[0]), .in_2(1'b0), .in_3(1'b0), .out(out_ari_left[1]));
  Multiplexer #(.Selector_Bits(2)) multiplexer_12 (
    .sel(shift), .in_0(in4[2]), .in_1(in4[1]), .in_2(in4[0]), .in_3(1'b0), .out(out_ari_left[2]));
  Multiplexer #(.Selector_Bits(2)) multiplexer_13 (
    .sel(shift), .in_0(in4[3]), .in_1(in4[2]), .in_2(in4[1]), .in_3(in4[0]), .out(out_ari_left[3]));
  Multiplexer #(.Selector_Bits(2)) multiplexer_14 (
    .sel(shift), .in_0(in4[0]), .in_1(in4[1]), .in_2(in4[2]), .in_3(in4[3]), .out(out_logic_right[0]));
  Multiplexer #(.Selector_Bits(2)) multiplexer_15 (
    .sel(shift), .in_0(in4[1]), .in_1(in4[2]), .in_2(in4[3]), .in_3(1'b0), .out(out_logic_right[1]));
  Multiplexer #(.Selector_Bits(2)) multiplexer_16 (
    .sel(shift), .in_0(in4[2]), .in_1(in4[3]), .in_2(1'b0), .in_3(1'b0), .out(out_logic_right[2]));
  Multiplexer #(.Selector_Bits(2)) multiplexer_17 (
    .sel(shift), .in_0(in4[3]), .in_1(1'b0), .in_2(1'b0), .in_3(1'b0), .out(out_logic_right[3]));
  Multiplexer #(.Selector_Bits(2)) multiplexer_18 (
    .sel(shift), .in_0(in4[0]), .in_1(in4[1]), .in_2(in4[2]), .in_3(in4[3]), .out(out_ari_right[0]));
  Multiplexer #(.Selector_Bits(2)) multiplexer_19 (
    .sel(shift), .in_0(in4[1]), .in_1(in4[2]), .in_2(in4[3]), .in_3(in4[3]), .out(out_ari_right[1]));
  Multiplexer #(.Selector_Bits(2)) multiplexer_20 (
    .sel(shift), .in_0(in4[2]), .in_1(in4[3]), .in_2(in4[3]), .in_3(in4[3]), .out(out_ari_right[2]));
  Multiplexer #(.Selector_Bits(2)) multiplexer_21 (
    .sel(shift), .in_0(in4[3]), .in_1(in4[3]), .in_2(in4[3]), .in_3(in4[3]), .out(out_ari_right[3]));

  // Other names for the same wires on the sheet: out_logic_left[3:0] = out_ari_left; in0 = in4[0]; in1 = in4[1];
  //   in2 = in4[2]; in3 = in4[3]; sign_byte = in4[3]

  // Notes on the sheet:
  //   Direction: left (0) or right (1)
  //   mode: 00 -> rotate
  //   01 -> logical
  //   10 -> arithmic
endmodule
