// Digital circuit barrel_shifter8.dig as structural Verilog
module barrel_shifter8 (
  input  [1:0] shift_byte,
  input  [31:0] in32,
  input  Direction,
  input  [1:0] mode,
  output [31:0] out32
);

  wire [7:0] sign_byte;
  wire [31:0] out_ari_left, out_ari_right, out_logic_right, out_rotate_left, out_rotate_right;

  Multiplexer #(.Selector_Bits(3), .Bits(32)) multiplexer_1 (
    .sel({mode, Direction}), .in_0(out_rotate_left), .in_1(out_rotate_right), .in_2(out_ari_left),
    .in_3(out_logic_right), .in_4(out_ari_left), .in_5(out_ari_right), .in_6({32{1'b0}}), .in_7({32{1'b0}}),
    .out(out32));
  BitExtender #(.inputBits(1), .outputBits(8)) bitextender_1 (.in(in32[31]), .out(sign_byte));
  Multiplexer #(.Selector_Bits(2), .Bits(8)) multiplexer_2 (
    .sel(shift_byte), .in_0(in32[7:0]), .in_1(in32[31:24]), .in_2(in32[23:16]), .in_3(in32[15:8]),
    .out(out_rotate_left[7:0]));
  Multiplexer #(.Selector_Bits(2), .Bits(8)) multiplexer_3 (
    .sel(shift_byte), .in_0(in32[15:8]), .in_1(in32[7:0]), .in_2(in32[31:24]), .in_3(in32[23:16]),
    .out(out_rotate_left[15:8]));
  Multiplexer #(.Selector_Bits(2), .Bits(8)) multiplexer_4 (
    .sel(shift_byte), .in_0(in32[23:16]), .in_1(in32[15:8]), .in_2(in32[7:0]), .in_3(in32[31:24]),
    .out(out_rotate_left[23:16]));
  Multiplexer #(.Selector_Bits(2), .Bits(8)) multiplexer_5 (
    .sel(shift_byte), .in_0(in32[31:24]), .in_1(in32[23:16]), .in_2(in32[15:8]), .in_3(in32[7:0]),
    .out(out_rotate_left[31:24]));
  Multiplexer #(.Selector_Bits(2), .Bits(8)) multiplexer_6 (
    .sel(shift_byte), .in_0(in32[7:0]), .in_1(in32[15:8]), .in_2(in32[23:16]), .in_3(in32[31:24]),
    .out(out_rotate_right[7:0]));
  Multiplexer #(.Selector_Bits(2), .Bits(8)) multiplexer_7 (
    .sel(shift_byte), .in_0(in32[15:8]), .in_1(in32[23:16]), .in_2(in32[31:24]), .in_3(in32[7:0]),
    .out(out_rotate_right[15:8]));
  Multiplexer #(.Selector_Bits(2), .Bits(8)) multiplexer_8 (
    .sel(shift_byte), .in_0(in32[23:16]), .in_1(in32[31:24]), .in_2(in32[7:0]), .in_3(in32[15:8]),
    .out(out_rotate_right[23:16]));
  Multiplexer #(.Selector_Bits(2), .Bits(8)) multiplexer_9 (
    .sel(shift_byte), .in_0(in32[31:24]), .in_1(in32[7:0]), .in_2(in32[15:8]), .in_3(in32[23:16]),
    .out(out_rotate_right[31:24]));
  Multiplexer #(.Selector_Bits(2), .Bits(8)) multiplexer_10 (
    .sel(shift_byte), .in_0(in32[7:0]), .in_1({8{1'b0}}), .in_2({8{1'b0}}), .in_3({8{1'b0}}),
    .out(out_ari_left[7:0]));
  Multiplexer #(.Selector_Bits(2), .Bits(8)) multiplexer_11 (
    .sel(shift_byte), .in_0(in32[15:8]), .in_1(in32[7:0]), .in_2({8{1'b0}}), .in_3({8{1'b0}}),
    .out(out_ari_left[15:8]));
  Multiplexer #(.Selector_Bits(2), .Bits(8)) multiplexer_12 (
    .sel(shift_byte), .in_0(in32[23:16]), .in_1(in32[15:8]), .in_2(in32[7:0]), .in_3({8{1'b0}}),
    .out(out_ari_left[23:16]));
  Multiplexer #(.Selector_Bits(2), .Bits(8)) multiplexer_13 (
    .sel(shift_byte), .in_0(in32[31:24]), .in_1(in32[23:16]), .in_2(in32[15:8]), .in_3(in32[7:0]),
    .out(out_ari_left[31:24]));
  Multiplexer #(.Selector_Bits(2), .Bits(8)) multiplexer_14 (
    .sel(shift_byte), .in_0(in32[7:0]), .in_1(in32[15:8]), .in_2(in32[23:16]), .in_3(in32[31:24]),
    .out(out_logic_right[7:0]));
  Multiplexer #(.Selector_Bits(2), .Bits(8)) multiplexer_15 (
    .sel(shift_byte), .in_0(in32[15:8]), .in_1(in32[23:16]), .in_2(in32[31:24]), .in_3({8{1'b0}}),
    .out(out_logic_right[15:8]));
  Multiplexer #(.Selector_Bits(2), .Bits(8)) multiplexer_16 (
    .sel(shift_byte), .in_0(in32[23:16]), .in_1(in32[31:24]), .in_2({8{1'b0}}), .in_3({8{1'b0}}),
    .out(out_logic_right[23:16]));
  Multiplexer #(.Selector_Bits(2), .Bits(8)) multiplexer_17 (
    .sel(shift_byte), .in_0(in32[31:24]), .in_1({8{1'b0}}), .in_2({8{1'b0}}), .in_3({8{1'b0}}),
    .out(out_logic_right[31:24]));
  Multiplexer #(.Selector_Bits(2), .Bits(8)) multiplexer_18 (
    .sel(shift_byte), .in_0(in32[7:0]), .in_1(in32[15:8]), .in_2(in32[23:16]), .in_3(in32[31:24]),
    .out(out_ari_right[7:0]));
  Multiplexer #(.Selector_Bits(2), .Bits(8)) multiplexer_19 (
    .sel(shift_byte), .in_0(in32[15:8]), .in_1(in32[23:16]), .in_2(in32[31:24]), .in_3(sign_byte),
    .out(out_ari_right[15:8]));
  Multiplexer #(.Selector_Bits(2), .Bits(8)) multiplexer_20 (
    .sel(shift_byte), .in_0(in32[23:16]), .in_1(in32[31:24]), .in_2(sign_byte), .in_3(sign_byte),
    .out(out_ari_right[23:16]));
  Multiplexer #(.Selector_Bits(2), .Bits(8)) multiplexer_21 (
    .sel(shift_byte), .in_0(in32[31:24]), .in_1(sign_byte), .in_2(sign_byte), .in_3(sign_byte),
    .out(out_ari_right[31:24]));

  // Other names for the same wires on the sheet: out_logic_left[31:0] = out_ari_left; inbyte0[7:0] = in32[7:0];
  //   inbyte1[7:0] = in32[15:8]; inbyte2[7:0] = in32[23:16]; inbyte3[7:0] = in32[31:24]

  // Notes on the sheet:
  //   Direction: left (0) or right (1)
  //   mode: 00 -> rotate
  //   01 -> logical
  //   10 -> arithmic
endmodule
