// Digital circuit csr.dig as structural Verilog
module csr (
  input  [5:0] CSRCode_in,
  input  [31:0] Data_in,
  input  [11:0] Csr_Addr,
  input  [4:0] Imm5_in,
  input  [31:0] Data_temp,
  input  Clock,
  output En,
  output [31:0] rd_out,
  output [31:0] Out_csr,
  output [11:0] Addr_csr
);

  wire [2:0] priorityencoder_1_num;
  wire [31:0] and_1_out, and_2_out, multiplexer_2_out, or_1_out, or_2_out, out_temp_q, pulldown_1_out,
       pulldown_2_out;

  PriorityEncoder #(.Selector_Bits(3)) priorityencoder_1 (
    .in0(CSRCode_in[0]), .in1(CSRCode_in[1]), .in2(CSRCode_in[2]), .in3(CSRCode_in[3]), .in4(CSRCode_in[4]),
    .in5(CSRCode_in[5]), .in6(1'b0), .in7(1'b0), .num(priorityencoder_1_num), .any(En));
  Register #(.Bits(32)) out_temp (.D(Data_temp), .C(Clock), .en(1'b1), .Q(out_temp_q));
  assign Addr_csr = En ? Csr_Addr : 12'bz;  // Driver driver_1
  PullDown #(.Bits(32)) pulldown_1 (.out(pulldown_1_out));
  Multiplexer #(.Bits(32)) multiplexer_1 (.sel(En), .in_0(pulldown_1_out), .in_1(out_temp_q), .out(rd_out));
  assign or_1_out = Data_in | rd_out;  // Or or_1, 32 bits wide
  assign and_1_out = ~Data_in & rd_out;  // And and_1, 32 bits wide
  assign or_2_out = {{27{1'b0}}, Imm5_in} | rd_out;  // Or or_2, 32 bits wide
  assign and_2_out = ~{{27{1'b0}}, Imm5_in} & rd_out;  // And and_2, 32 bits wide
  Multiplexer #(.Selector_Bits(3), .Bits(32)) multiplexer_2 (
    .sel(priorityencoder_1_num), .in_0(Data_in), .in_1(or_1_out), .in_2(and_1_out),
    .in_3({{27{1'b0}}, Imm5_in}), .in_4(or_2_out), .in_5(and_2_out), .in_6(pulldown_2_out),
    .in_7(pulldown_2_out), .out(multiplexer_2_out));
  PullDown #(.Bits(32)) pulldown_2 (.out(pulldown_2_out));
  assign Out_csr = En ? multiplexer_2_out : 32'bz;  // Driver driver_2

  // Other names for the same wires on the sheet: csrrw = CSRCode_in[0]; csrrs = CSRCode_in[1]; csrrc = CSRCode_in[2];
  //   csrrwi = CSRCode_in[3]; csrrsi = CSRCode_in[4]; csrrci = CSRCode_in[5]
endmodule
