// Digital circuit csr_addr_spliter.dig as structural Verilog
module csr_addr_spliter (
  input  [11:0] Addr_csr,
  output [2:0] LUT_out
);

  wire [3:3] lookuptable_1_out;

  LookUpTable #(.Bits(4)) lookuptable_1 (
    .in0(Addr_csr[0]), .in1(Addr_csr[1]), .in2(Addr_csr[2]), .in3(Addr_csr[3]), .in4(Addr_csr[4]),
    .in5(Addr_csr[5]), .in6(Addr_csr[6]), .in7(Addr_csr[7]), .in8(Addr_csr[8]), .in9(Addr_csr[9]),
    .in10(Addr_csr[10]), .in11(Addr_csr[11]), .out({lookuptable_1_out[3], LUT_out}));

  // Other names for the same wires on the sheet: w0 = Addr_csr[0]; w1 = Addr_csr[1]; w2 = Addr_csr[2];
  //   w3 = Addr_csr[3]; w4 = Addr_csr[4]; w5 = Addr_csr[5]; w6 = Addr_csr[6]; w7 = Addr_csr[7]; w8 = Addr_csr[8];
  //   w9 = Addr_csr[9]; w10 = Addr_csr[10]; w11 = Addr_csr[11]

  // Notes on the sheet:
  //   contents of lookuptable_1 (hex, n*v repeats v):
  //   768*0,1,0,0,0,2,3,59*0,4,5,6,7
endmodule
