// Digital circuit debug.dig as structural Verilog
module debug (
  input  EN,
  input  C_in,
  input  man,
  input  [31:0] PC_cur,
  output clock
);

  wire comparator_1_lt, multiplexer_1_out;

  Comparator #(.Bits(32)) comparator_1 (.a(PC_cur), .b(32'h40000000), .lt(comparator_1_lt));  // open: gt, eq
  Multiplexer multiplexer_1 (.sel(EN), .in_0(1'b0), .in_1(comparator_1_lt), .out(multiplexer_1_out));
  Multiplexer multiplexer_2 (.sel(multiplexer_1_out), .in_0(C_in), .in_1(man), .out(clock));

  // Notes on the sheet:
  //   C_in: Hz: 100
  //   man: manual clock
endmodule
