// Digital circuit decoder_2bit.dig as structural Verilog
module decoder_2bit (
  input  EN,
  input  Din,
  output _0,
  output _1
);

  wire [1:0] decoder_1_out_0;

  Decoder decoder_1 (.sel(Din), .out_0(decoder_1_out_0[0]), .out_1(decoder_1_out_0[1]));
  Multiplexer #(.Bits(2)) multiplexer_1 (.sel(EN), .in_0(2'b00), .in_1(decoder_1_out_0), .out({_1, _0}));
endmodule
