// Digital circuit decoder_3bit.dig as structural Verilog
module decoder_3bit (
  input  EN,
  input  [2:0] Din,
  output _0,
  output _1,
  output _2,
  output _3,
  output _4,
  output _5,
  output _6,
  output _7
);

  wire [7:0] decoder_1_out_0;

  Decoder #(.Selector_Bits(3)) decoder_1 (
    .sel(Din), .out_0(decoder_1_out_0[0]), .out_1(decoder_1_out_0[1]), .out_2(decoder_1_out_0[2]),
    .out_3(decoder_1_out_0[3]), .out_4(decoder_1_out_0[4]), .out_5(decoder_1_out_0[5]),
    .out_6(decoder_1_out_0[6]), .out_7(decoder_1_out_0[7]));
  Multiplexer #(.Bits(8)) multiplexer_1 (
    .sel(EN), .in_0({8{1'b0}}), .in_1(decoder_1_out_0), .out({_7, _6, _5, _4, _3, _2, _1, _0}));
endmodule
