// Digital circuit gpio.dig as structural Verilog
module gpio (
  input  Clock,
  input  [31:0] Addr_w,
  input  [31:0] Data_in,
  input  we,
  input  [31:0] Addr_rd,
  input  int_gate,
  input  GPIO1_in,
  input  GPIO2_in,
  input  GPIO3_in,
  input  GPIO4_in,
  input  GPIO5_in,
  input  GPIO6_in,
  input  GPIO7_in,
  input  GPIO8_in,
  input  GPIO9_in,
  input  GPIO10_in,
  output [31:0] Out_rd,
  output Out_en,
  output [31:0] perint_code,
  output GPIO1_out,
  output GPIO2_out,
  output GPIO3_out,
  output GPIO4_out,
  output GPIO5_out,
  output GPIO6_out,
  output GPIO7_out,
  output GPIO8_out,
  output GPIO9_out,
  output GPIO10_out
);

  wire addr_compare_1_p3, addr_compare_2_p3, and_3_out, code_en, comparator_1_eq, comparator_2_eq, nor_1_out;
  wire [2:0] addr2reg_num_1_reg_num;
  wire [7:0] addr2reg_num_2_one_hot;
  wire [9:0] and_1_out, and_2_out, and_4_out, and_5_out, gpio_value1, multiplexer_2_out, or_1_out;
  wire [31:0] cur_gpioset, cur_gpiovalue, int_code, int_codein, multiplexer_1_out, pulldown_1_out;

  addr2reg_num addr2reg_num_1 (
    .Addr(Addr_rd), .Addr_base(32'ha0000000), .EN(we), .num(3'b011), .REG_num(addr2reg_num_1_reg_num),
    .OE(Out_en));  // open: one_hot
  addr2reg_num addr2reg_num_2 (
    .Addr(Addr_w), .Addr_base(32'ha0000000), .EN(we), .num(3'b011), .one_hot(addr2reg_num_2_one_hot));  // open: REG_num, OE
  Multiplexer #(.Selector_Bits(3), .Bits(32)) multiplexer_1 (
    .sel(addr2reg_num_1_reg_num), .in_0(cur_gpioset), .in_1(cur_gpiovalue), .in_2(int_code),
    .in_3(pulldown_1_out), .in_4(pulldown_1_out), .in_5(pulldown_1_out), .in_6(pulldown_1_out),
    .in_7(pulldown_1_out), .out(multiplexer_1_out));
  PullDown #(.Bits(32)) pulldown_1 (.out(pulldown_1_out));
  Register #(.Bits(32)) config_reg (.D(Data_in), .C(Clock), .en(addr2reg_num_2_one_hot[0]), .Q(cur_gpioset));
  assign Out_rd = Out_en ? multiplexer_1_out : 32'bz;  // Driver driver_1
  assign and_1_out = Data_in[9:0] & cur_gpioset[9:0];  // And and_1, 10 bits wide
  assign and_2_out = gpio_value1 & ~cur_gpioset[9:0];  // And and_2, 10 bits wide
  assign or_1_out = and_1_out | and_2_out;  // Or or_1, 10 bits wide
  Multiplexer #(.Bits(10)) multiplexer_2 (
    .sel(addr2reg_num_2_one_hot[1]), .in_0(gpio_value1), .in_1(or_1_out), .out(multiplexer_2_out));
  Register #(.Bits(32)) data_reg (.D({{22{1'b0}}, multiplexer_2_out}), .C(Clock), .en(1'b1), .Q(cur_gpiovalue));
  // addr_compare addr_compare_1: pin names not known; wires that end beside it: Addr_w, 32'ha0000008, addr_compare_1_p3
  Comparator #(.Bits(10)) comparator_1 (.a(gpio_value1), .b(cur_gpiovalue[9:0]), .eq(comparator_1_eq));  // open: gt, lt
  Comparator #(.Bits(32)) comparator_2 (.a(int_code), .b({32{1'b0}}), .eq(comparator_2_eq));  // open: gt, lt
  nor nor_1 (nor_1_out, int_gate, comparator_1_eq);
  and and_3 (and_3_out, ~comparator_2_eq, we, addr_compare_1_p3);  // And
  assign and_4_out = {GPIO10_in, GPIO9_in, GPIO8_in, GPIO7_in, GPIO6_in, GPIO5_in, GPIO4_in, GPIO3_in, GPIO2_in, GPIO1_in} & ~cur_gpioset[9:0];  // And and_4, 10 bits wide
  assign and_5_out = cur_gpioset[9:0] & cur_gpiovalue[9:0];  // And and_5, 10 bits wide
  // addr_compare addr_compare_2: pin names not known; wires that end beside it: int_code, {32{1'b0}}, addr_compare_2_p3
  assign int_codein = nor_1_out ? 32'h1 : 32'bz;  // Driver driver_2
  assign int_codein = and_3_out ? Data_in : 32'bz;  // Driver driver_3
  assign gpio_value1 = and_4_out | and_5_out;  // Or or_2, 10 bits wide
  assign perint_code = ~addr_compare_2_p3 ? int_code : 32'bz;  // DriverInvSel driverinvsel_1
  assign code_en = nor_1_out ? 1'b1 : 1'bz;  // Driver driver_4
  assign code_en = and_3_out ? 1'b1 : 1'bz;  // Driver driver_5
  PullDown pulldown_2 (.out(code_en));
  assign {GPIO10_out, GPIO9_out, GPIO8_out, GPIO7_out, GPIO6_out, GPIO5_out, GPIO4_out, GPIO3_out, GPIO2_out, GPIO1_out} = cur_gpiovalue[9:0] & cur_gpioset[9:0];  // And and_6, 10 bits wide
  Register #(.Bits(32)) register_1 (.D(int_codein), .C(Clock), .en(code_en), .Q(int_code));

  // Other names for the same wires on the sheet: GPIOOUT_1 = GPIO1_out; GPIOOUT_2 = GPIO2_out; GPIOOUT_3 = GPIO3_out;
  //   GPIOOUT_4 = GPIO4_out; GPIOOUT_5 = GPIO5_out; GPIOOUT_6 = GPIO6_out; GPIOOUT_7 = GPIO7_out;
  //   GPIOOUT_8 = GPIO8_out; GPIOOUT_9 = GPIO9_out; GPIOOUT_10 = GPIO10_out; C = Clock;
  //   gpio_settmp[9:0] = cur_gpioset[9:0]; cur_gpiovaluetemp[9:0] = cur_gpiovalue[9:0]; GPIOIN_1 = GPIO1_in;
  //   GPIOIN_2 = GPIO2_in; GPIOIN_3 = GPIO3_in; GPIOIN_4 = GPIO4_in; GPIOIN_5 = GPIO5_in; GPIOIN_6 = GPIO6_in;
  //   GPIOIN_7 = GPIO7_in; GPIOIN_8 = GPIO8_in; GPIOIN_9 = GPIO9_in; GPIOIN_10 = GPIO10_in
endmodule
