// Digital circuit instruction_decoder.dig as structural Verilog
module instruction_decoder (
  input  [31:0] Instruction_In,
  input  EN,
  output [4:0] rd,
  output [4:0] rs1,
  output [4:0] rs2,
  output [6:0] imm_2531,
  output [19:0] imm_1231,
  output [11:0] imm_2032,
  output [31:0] invalid,
  output [5:0] csr_op,
  output [8:0] jmp_op,
  output [18:0] alu_op,
  output [8:0] mem_op,
  output [7:0] machine_op,
  output cust_op
);

  wire and_1_out, and_2_out, and_3_out, comparator_4_eq, decoder_1_out_1, decoder_1_out_2, decoder_1_out_3,
       decoder_1_out_5, decoder_1_out_7, decoder_1_out_8, decoder_1_out_11, decoder_3bit_1__2,
       decoder_3bit_1__3, decoder_3bit_1__4, decoder_3bit_1__5, decoder_3bit_1__6, decoder_3bit_1__7,
       decoder_3bit_2__3, decoder_3bit_2__4, decoder_3bit_2__5, decoder_3bit_2__6, decoder_3bit_2__7,
       decoder_3bit_3__0, decoder_3bit_3__5, decoder_3bit_4__3, decoder_3bit_4__6, decoder_3bit_4__7,
       decoder_3bit_5__2, decoder_3bit_5__3, decoder_3bit_6__5, decoder_3bit_7__0, invalid_op0, invalid_op1,
       invalid_op3, invalid_op5, invalid_op8, invalid_op11, nor_1_out, or_5_out;
  wire [3:0] LUT_inst_Decoder_out;
  wire [6:0] multiplexer_1_out;

  Multiplexer #(.Bits(32)) multiplexer_1 (
    .sel(EN), .in_0({32{1'b0}}), .in_1(Instruction_In), .out({imm_1231, rd, multiplexer_1_out}));
  Comparator #(.Bits(32)) comparator_1 (
    .a({imm_1231, rd, multiplexer_1_out}), .b(32'h10200073), .eq(machine_op[4]));  // open: gt, lt
  Comparator #(.Bits(32)) comparator_2 (
    .a({imm_1231, rd, multiplexer_1_out}), .b(32'h30200073), .eq(machine_op[2]));  // open: gt, lt
  Comparator #(.Bits(32)) comparator_3 (
    .a({imm_1231, rd, multiplexer_1_out}), .b(32'h10500073), .eq(machine_op[5]));  // open: gt, lt
  LookUpTable #(.Bits(4)) LUT_inst_Decoder (
    .in0(multiplexer_1_out[0]), .in1(multiplexer_1_out[1]), .in2(multiplexer_1_out[2]),
    .in3(multiplexer_1_out[3]), .in4(multiplexer_1_out[4]), .in5(multiplexer_1_out[5]),
    .in6(multiplexer_1_out[6]), .out(LUT_inst_Decoder_out));
  Decoder #(.Selector_Bits(4)) decoder_1 (
    .sel(LUT_inst_Decoder_out), .out_0(invalid_op0), .out_1(decoder_1_out_1), .out_2(decoder_1_out_2),
    .out_3(decoder_1_out_3), .out_4(jmp_op[1]), .out_5(decoder_1_out_5), .out_6(jmp_op[0]),
    .out_7(decoder_1_out_7), .out_8(decoder_1_out_8), .out_9(jmp_op[8]), .out_10(mem_op[0]),
    .out_11(decoder_1_out_11), .out_15(cust_op));  // open: out_12, out_13, out_14
  decoder_3bit decoder_3bit_1 (
    .EN(decoder_1_out_11), .Din(imm_1231[2:0]), ._0(machine_op[6]), ._1(machine_op[7]),
    ._2(decoder_3bit_1__2), ._3(decoder_3bit_1__3), ._4(decoder_3bit_1__4), ._5(decoder_3bit_1__5),
    ._6(decoder_3bit_1__6), ._7(decoder_3bit_1__7));
  decoder_3bit decoder_3bit_2 (
    .EN(decoder_1_out_8), .Din(imm_1231[2:0]), ._0(mem_op[6]), ._1(mem_op[7]), ._2(mem_op[8]),
    ._3(decoder_3bit_2__3), ._4(decoder_3bit_2__4), ._5(decoder_3bit_2__5), ._6(decoder_3bit_2__6),
    ._7(decoder_3bit_2__7));
  decoder_3bit decoder_3bit_3 (
    .EN(decoder_1_out_7), .Din(imm_1231[2:0]), ._0(decoder_3bit_3__0), ._1(alu_op[2]), ._2(alu_op[3]),
    ._3(alu_op[4]), ._4(alu_op[5]), ._5(decoder_3bit_3__5), ._6(alu_op[8]), ._7(alu_op[9]));
  decoder_3bit decoder_3bit_4 (
    .EN(decoder_1_out_5), .Din(imm_1231[2:0]), ._0(mem_op[1]), ._1(mem_op[2]), ._2(mem_op[3]),
    ._3(decoder_3bit_4__3), ._4(mem_op[4]), ._5(mem_op[5]), ._6(decoder_3bit_4__6), ._7(decoder_3bit_4__7));
  decoder_3bit decoder_3bit_5 (
    .EN(decoder_1_out_1), .Din(imm_1231[2:0]), ._0(jmp_op[2]), ._1(jmp_op[3]), ._2(decoder_3bit_5__2),
    ._3(decoder_3bit_5__3), ._4(jmp_op[4]), ._5(jmp_op[5]), ._6(jmp_op[6]), ._7(jmp_op[7]));
  decoder_3bit decoder_3bit_6 (
    .EN(decoder_1_out_2), .Din(imm_1231[2:0]), ._0(alu_op[10]), ._1(alu_op[11]), ._2(alu_op[12]),
    ._3(alu_op[13]), ._4(alu_op[14]), ._5(decoder_3bit_6__5), ._6(alu_op[17]), ._7(alu_op[18]));
  decoder_3bit decoder_3bit_7 (
    .EN(decoder_1_out_3), .Din(imm_1231[2:0]), ._0(decoder_3bit_7__0), ._1(csr_op[0]), ._2(csr_op[1]),
    ._3(csr_op[2]), ._4(invalid_op3), ._5(csr_op[3]), ._6(csr_op[4]), ._7(csr_op[5]));
  or or_1 (invalid_op8, decoder_3bit_2__3, decoder_3bit_2__4, decoder_3bit_2__5, decoder_3bit_2__6, decoder_3bit_2__7);
  or or_2 (invalid_op11, decoder_3bit_1__2, decoder_3bit_1__3, decoder_3bit_1__4, decoder_3bit_1__5, decoder_3bit_1__6, decoder_3bit_1__7);
  decoder_2bit decoder_2bit_1 (.EN(decoder_3bit_3__0), .Din(imm_1231[18]), ._0(alu_op[0]), ._1(alu_op[1]));
  decoder_2bit decoder_2bit_2 (.EN(decoder_3bit_3__5), .Din(imm_1231[18]), ._0(alu_op[7]), ._1(alu_op[6]));
  or or_3 (invalid_op5, decoder_3bit_4__3, decoder_3bit_4__6, decoder_3bit_4__7);
  or or_4 (invalid_op1, decoder_3bit_5__2, decoder_3bit_5__3);
  decoder_2bit decoder_2bit_3 (.EN(decoder_3bit_6__5), .Din(imm_1231[18]), ._0(alu_op[15]), ._1(alu_op[16]));
  nor nor_1 (nor_1_out, imm_1231[13], imm_1231[14], imm_1231[15], imm_1231[16], imm_1231[17], imm_1231[18], imm_1231[19], imm_1231[12], imm_1231[11], imm_1231[10], imm_1231[9]);
  and and_1 (and_1_out, nor_1_out, imm_1231[8]);
  and and_2 (and_2_out, nor_1_out, ~imm_1231[8]);  // And
  Comparator #(.Bits(7)) comparator_4 (.a(imm_1231[19:13]), .b(7'b0001001), .eq(comparator_4_eq));  // open: gt, lt
  Multiplexer multiplexer_2 (.sel(decoder_3bit_7__0), .in_0(1'b0), .in_1(and_2_out), .out(machine_op[1]));
  Multiplexer multiplexer_3 (.sel(decoder_3bit_7__0), .in_0(1'b0), .in_1(comparator_4_eq), .out(machine_op[3]));
  Multiplexer multiplexer_4 (.sel(decoder_3bit_7__0), .in_0(1'b0), .in_1(and_1_out), .out(machine_op[0]));
  or or_5 (or_5_out, invalid_op0, invalid_op1, invalid_op3, invalid_op5, invalid_op8, invalid_op11);
  and and_3 (and_3_out, EN, or_5_out);
  assign invalid = and_3_out ? 32'h2 : 32'bz;  // Driver driver_1

  assign imm_2032 = imm_1231[19:8];
  assign imm_2531 = imm_1231[19:13];
  assign rs1 = imm_1231[7:3];
  assign rs2 = imm_1231[12:8];

  // Other names for the same wires on the sheet: funct3[2:0] = imm_1231[2:0]; imm_12_31[19:0] = imm_1231;
  //   imm_20_31[11:0] = imm_1231[19:8]; imm_25_31[6:0] = imm_1231[19:13]; _30 = imm_1231[18]; add = alu_op[0];
  //   addi = alu_op[10]; and = alu_op[9]; andi = alu_op[18]; auipc = jmp_op[8]; beq = jmp_op[2]; bge = jmp_op[5];
  //   bgeu = jmp_op[7]; blt = jmp_op[4]; bltu = jmp_op[6]; bne = jmp_op[3]; csrrc = csr_op[2]; csrrci = csr_op[5];
  //   csrrs = csr_op[1]; csrrsi = csr_op[4]; csrrw = csr_op[0]; csrrwi = csr_op[3]; ebreak = machine_op[0];
  //   ecall = machine_op[1]; fence = machine_op[6]; fence_i = machine_op[7]; jal = jmp_op[0]; jalr = jmp_op[1];
  //   lb = mem_op[1]; lbu = mem_op[4]; lh = mem_op[2]; lhu = mem_op[5]; lui = mem_op[0]; lw = mem_op[3];
  //   mret = machine_op[2]; or = alu_op[8]; ori = alu_op[17]; sb = mem_op[6]; sfence_vma = machine_op[3];
  //   sh = mem_op[7]; sll = alu_op[2]; slli = alu_op[11]; slt = alu_op[3]; slti = alu_op[12]; sltiu = alu_op[13];
  //   sltu = alu_op[4]; sra = alu_op[6]; srai = alu_op[16]; sret = machine_op[4]; srl = alu_op[7]; srli = alu_op[15];
  //   sub = alu_op[1]; sw = mem_op[8]; wfi = machine_op[5]; xor = alu_op[5]; xori = alu_op[14]

  // Notes on the sheet:
  //   contents of LUT_inst_Decoder (hex, n*v repeats v):
  //   0,0,0,5,11*0,b,0,0,0,2,0,0,0,9,11*0,8,15*0,7,0,0,0,a,43*0,1,0,0,0
  //   ,4,7*0,6,0,0,0,3,11*0,f
  //   U
  //   R
  //   I
  //   B
  //   S
endmodule
