// Digital circuit instuction_jump_unit.dig as structural Verilog
module instuction_jump_unit (
  input  [8:0] jmp_op,
  input  [31:0] PC_cur,
  input  [31:0] rs1_in,
  input  [31:0] rs2_in,
  input  [11:0] Imm12_in,
  input  [19:0] Imm20_in,
  input  [6:0] Imm7_in,
  input  [4:0] offset_5,
  output EN_out,
  output [31:0] rd_out,
  output [31:0] Addr_jmp,
  output En_jmp
);

  wire multiplexer_3_out, multiplexer_7_out, not_1_out, or_1_out, or_2_out, priorityencoder_1_any,
       pulldown_3_out, pulldown_5_out, pulldown_7_out, pulldown_9_out, Signed_eq, Signed_gt, Signed_lt,
       Unsigned_eq, Unsigned_gt, Unsigned_lt;
  wire [3:0] priorityencoder_1_num;
  wire [31:0] add_1_s, add_2_s, add_3_s, add_4_s, Addr_offset, barrelshifter_1_out, bitextender_1_out,
       bitextender_2_out, bitextender_3_out, bitextender_4_out, multiplexer_1_out, multiplexer_5_out,
       multiplexer_8_out, pulldown_1_out, pulldown_2_out, pulldown_4_out, pulldown_6_out, pulldown_8_out;

  BitExtender #(.inputBits(20), .outputBits(32)) bitextender_1 (.in(Imm20_in), .out(bitextender_1_out));
  PriorityEncoder #(.Selector_Bits(4)) priorityencoder_1 (
    .in0(jmp_op[0]), .in1(jmp_op[1]), .in2(jmp_op[2]), .in3(jmp_op[3]), .in4(jmp_op[4]), .in5(jmp_op[5]),
    .in6(jmp_op[6]), .in7(jmp_op[7]), .in8(jmp_op[8]), .in9(1'b0), .in10(1'b0), .in11(1'b0), .in12(1'b0),
    .in13(1'b0), .in14(1'b0), .in15(1'b0), .num(priorityencoder_1_num), .any(priorityencoder_1_any));
  BitExtender #(.inputBits(21), .outputBits(32)) bitextender_2 (
    .in({Imm20_in[19], Imm20_in[7:0], Imm20_in[8], Imm20_in[18:9], 1'b0}), .out(bitextender_2_out));
  BitExtender #(.inputBits(12), .outputBits(32)) bitextender_3 (.in(Imm12_in), .out(bitextender_3_out));
  BitExtender #(.inputBits(13), .outputBits(32)) bitextender_4 (
    .in({Imm7_in[6], offset_5[0], Imm7_in[5:0], offset_5[4:1], 1'b0}), .out(bitextender_4_out));
  BarrelShifter #(.Bits(32)) barrelshifter_1 (.in(bitextender_1_out), .shift(6'b001100), .out(barrelshifter_1_out));
  PullDown #(.Bits(32)) pulldown_1 (.out(pulldown_1_out));
  Comparator #(.Signed("true"), .Bits(32)) Signed (
    .a(rs1_in), .b(rs2_in), .gt(Signed_gt), .eq(Signed_eq), .lt(Signed_lt));
  Comparator #(.Signed("true"), .Bits(32)) Unsigned (
    .a(rs1_in), .b(rs2_in), .gt(Unsigned_gt), .eq(Unsigned_eq), .lt(Unsigned_lt));
  Multiplexer #(.Selector_Bits(4), .Bits(32)) multiplexer_1 (
    .sel(priorityencoder_1_num), .in_0(bitextender_2_out), .in_1(bitextender_3_out),
    .in_2(bitextender_4_out), .in_3(bitextender_4_out), .in_4(bitextender_4_out), .in_5(bitextender_4_out),
    .in_6(bitextender_4_out), .in_7(bitextender_4_out), .in_8(barrelshifter_1_out), .in_9(pulldown_1_out),
    .in_10(pulldown_1_out), .in_11(pulldown_1_out), .in_12(pulldown_1_out), .in_13(pulldown_1_out),
    .in_14(pulldown_1_out), .in_15(pulldown_1_out), .out(multiplexer_1_out));
  Multiplexer #(.Bits(32)) multiplexer_2 (
    .sel(priorityencoder_1_any), .in_0(pulldown_2_out), .in_1(multiplexer_1_out), .out(Addr_offset));
  PullDown #(.Bits(32)) pulldown_2 (.out(pulldown_2_out));
  or or_1 (or_1_out, Signed_gt, Signed_eq);
  or or_2 (or_2_out, Unsigned_gt, Unsigned_eq);
  Add #(.Bits(32)) add_1 (.a(Addr_offset), .b(rs1_in), .c_i(1'b0), .s(add_1_s));  // open: c_o
  Add #(.Bits(32)) add_2 (.a(Addr_offset), .b(PC_cur), .c_i(1'b0), .s(add_2_s));  // open: c_o
  Multiplexer #(.Selector_Bits(4)) multiplexer_3 (
    .sel(priorityencoder_1_num), .in_0(1'b1), .in_1(1'b1), .in_2(Signed_eq), .in_3(not_1_out),
    .in_4(Signed_lt), .in_5(or_1_out), .in_6(Unsigned_lt), .in_7(or_2_out), .in_8(pulldown_3_out),
    .in_9(pulldown_3_out), .in_10(pulldown_3_out), .in_11(pulldown_3_out), .in_12(pulldown_3_out),
    .in_13(pulldown_3_out), .in_14(pulldown_3_out), .in_15(pulldown_3_out), .out(multiplexer_3_out));
  not not_1 (not_1_out, Unsigned_eq);
  PullDown pulldown_3 (.out(pulldown_3_out));
  PullDown #(.Bits(32)) pulldown_4 (.out(pulldown_4_out));
  Multiplexer multiplexer_4 (
    .sel(priorityencoder_1_any), .in_0(pulldown_5_out), .in_1(multiplexer_3_out), .out(En_jmp));
  PullDown pulldown_5 (.out(pulldown_5_out));
  Multiplexer #(.Selector_Bits(4), .Bits(32)) multiplexer_5 (
    .sel(priorityencoder_1_num), .in_0(add_2_s), .in_1(add_1_s), .in_2(add_2_s), .in_3(add_2_s),
    .in_4(add_2_s), .in_5(add_2_s), .in_6(add_2_s), .in_7(add_2_s), .in_8(add_2_s), .in_9(pulldown_4_out),
    .in_10(pulldown_4_out), .in_11(pulldown_4_out), .in_12(pulldown_4_out), .in_13(pulldown_4_out),
    .in_14(pulldown_4_out), .in_15(pulldown_4_out), .out(multiplexer_5_out));
  Multiplexer #(.Bits(32)) multiplexer_6 (
    .sel(priorityencoder_1_any), .in_0(pulldown_6_out), .in_1(multiplexer_5_out), .out(Addr_jmp));
  PullDown #(.Bits(32)) pulldown_6 (.out(pulldown_6_out));
  Add #(.Bits(32)) add_3 (.a(PC_cur), .b(32'h4), .c_i(1'b0), .s(add_3_s));  // open: c_o
  Add #(.Bits(32)) add_4 (.a(Addr_offset), .b(PC_cur), .c_i(1'b0), .s(add_4_s));  // open: c_o
  PullDown pulldown_7 (.out(pulldown_7_out));
  PullDown #(.Bits(32)) pulldown_8 (.out(pulldown_8_out));
  Multiplexer #(.Selector_Bits(4)) multiplexer_7 (
    .sel(priorityencoder_1_num), .in_0(1'b1), .in_1(1'b1), .in_2(pulldown_7_out), .in_3(pulldown_7_out),
    .in_4(pulldown_7_out), .in_5(pulldown_7_out), .in_6(pulldown_7_out), .in_7(pulldown_7_out), .in_8(1'b1),
    .in_9(pulldown_7_out), .in_10(pulldown_7_out), .in_11(pulldown_7_out), .in_12(pulldown_7_out),
    .in_13(pulldown_7_out), .in_14(pulldown_7_out), .in_15(pulldown_7_out), .out(multiplexer_7_out));
  Multiplexer #(.Selector_Bits(4), .Bits(32)) multiplexer_8 (
    .sel(priorityencoder_1_num), .in_0(add_3_s), .in_1(add_3_s), .in_2(pulldown_8_out),
    .in_3(pulldown_8_out), .in_4(pulldown_8_out), .in_5(pulldown_8_out), .in_6(pulldown_8_out),
    .in_7(pulldown_8_out), .in_8(add_4_s), .in_9(pulldown_8_out), .in_10(pulldown_8_out),
    .in_11(pulldown_8_out), .in_12(pulldown_8_out), .in_13(pulldown_8_out), .in_14(pulldown_8_out),
    .in_15(pulldown_8_out), .out(multiplexer_8_out));
  Multiplexer multiplexer_9 (
    .sel(priorityencoder_1_any), .in_0(pulldown_9_out), .in_1(multiplexer_7_out), .out(EN_out));
  PullDown pulldown_9 (.out(pulldown_9_out));
  assign rd_out = priorityencoder_1_any ? multiplexer_8_out : 32'bz;  // Driver driver_1

  // Other names for the same wires on the sheet: jal = jmp_op[0]; jalr = jmp_op[1]; beq = jmp_op[2]; bne = jmp_op[3];
  //   blt = jmp_op[4]; bge = jmp_op[5]; bltu = jmp_op[6]; bgeu = jmp_op[7]; auipc = jmp_op[8]; rs1[31:0] = rs1_in;
  //   rs2[31:0] = rs2_in
endmodule
