// Digital circuit int_except_unit.dig as structural Verilog
module int_except_unit (
  input  WE_CSR,
  input  [31:0] Data_csr,
  input  [11:0] Addr_csrw,
  input  [11:0] Addr_csr1,
  input  [11:0] Addr_csr2,
  input  [31:0] Exception_code,
  input  [31:0] PC_Addr,
  input  [31:0] PC_ip,
  input  [31:0] PC_next,
  input  mret,
  input  mip_en,
  input  [31:0] mip_in,
  input  Clock,
  output [31:0] Out_csr1,
  output [31:0] Out_csr2,
  output En_jmp,
  output [31:0] Addr_jmp,
  output [31:0] mip_out,
  output [31:0] mie_out,
  output [31:0] ecode_out,
  output timer_en,
  output [31:0] mepc_out
);

  wire and_3_out, and_7_out, and_8_out, and_10_out, and_11_out, and_12_out, and_13_out, and_14_out,
       and_15_out, and_16_out, demultiplexer_3_out_0, demultiplexer_3_out_1, demultiplexer_3_out_4,
       demultiplexer_3_out_5, demultiplexer_3_out_6, Do_intperipheral, Do_intsoft, Do_inttimer, driver_2_out,
       EN_excep, EN_ie, enter_excep, int_peripheral, int_soft, int_timer, mcause_en, mepc_en, mie_en,
       mstatus_en, mtval, mtvec_en, not_2_out, or_1_out, or_2_out, or_3_out, or_4_out, or_5_out;
  wire [2:0] csr_addr_spliter_1_lut_out, csr_addr_spliter_2_lut_out, csr_addr_spliter_3_lut_out;
  wire [11:0] demultiplexer_1_out_0;
  wire [30:0] lookuptable_1_out;
  wire [31:0] add_2_s, and_2_out, CSR_Registers_da, CSR_Registers_db, demultiplexer_2_out_0,
       demultiplexer_2_out_1, demultiplexer_2_out_4, demultiplexer_2_out_5, demultiplexer_2_out_6,
       driver_1_out, mcause_data, mcause_in, mcause_out, mepc_data, mepc_in, mepc_out_t, mie_in, mstatus_in,
       mstatus_out, mtval_in, mtval_out, mtvec_in, mtvec_out, multiplexer_1_out, offset_jmp, pc_reg_q,
       pcnext_reg_q, vec_offset;

  or or_1 (or_1_out, enter_excep, mret);
  and and_1 (En_jmp, or_1_out, 1'b1);
  Register #(.Bits(32)) mstatus (
    .D(mstatus_in), .C(Clock), .en(mstatus_en), .Q({mstatus_out[31:4], EN_ie, mstatus_out[2:0]}));
  Register #(.Bits(32)) mcause (.D(mcause_in), .C(Clock), .en(mcause_en), .Q(mcause_out));
  csr_addr_spliter csr_addr_spliter_1 (.Addr_csr(Addr_csrw), .LUT_out(csr_addr_spliter_1_lut_out));
  Register #(.Bits(32)) mie (.D(mie_in), .C(Clock), .en(mie_en), .Q(mie_out));
  Register #(.Bits(32)) u_mtval (.D(mtval_in), .C(Clock), .en(mtval), .Q(mtval_out));
  Demultiplexer #(.Selector_Bits(3), .Bits(12)) demultiplexer_1 (
    .sel(csr_addr_spliter_1_lut_out), .in(Addr_csrw), .out_0(demultiplexer_1_out_0));  // open: out_1, out_2, out_3, out_4, out_5, out_6, out_7
  Register #(.Bits(32)) mtvec (.D(mtvec_in), .C(Clock), .en(mtvec_en), .Q(mtvec_out));
  Demultiplexer #(.Selector_Bits(3), .Bits(32)) demultiplexer_2 (
    .sel(csr_addr_spliter_1_lut_out), .in(Data_csr), .out_0(demultiplexer_2_out_0),
    .out_1(demultiplexer_2_out_1), .out_2(mie_in), .out_3(mtvec_in), .out_4(demultiplexer_2_out_4),
    .out_5(demultiplexer_2_out_5), .out_6(demultiplexer_2_out_6));  // open: out_7
  assign driver_1_out = mip_en ? mip_in : 32'bz;  // Driver driver_1
  assign driver_2_out = mip_en ? 1'b1 : 1'bz;  // Driver driver_2
  Register #(.Bits(32)) mip (.D(driver_1_out), .C(Clock), .en(driver_2_out), .Q(mip_out));
  PullUp #(.Bits(32)) pullup_1 (.out(Exception_code));
  Multiplexer #(.Bits(32)) multiplexer_1 (
    .sel(enter_excep), .in_0(demultiplexer_2_out_1),
    .in_1({mstatus_out[31:8], EN_ie, mstatus_out[6:4], 1'b0, mstatus_out[2:0]}), .out(multiplexer_1_out));
  Multiplexer #(.Bits(32)) multiplexer_2 (
    .sel(enter_excep), .in_0(demultiplexer_2_out_4), .in_1(mepc_data), .out(mepc_in));
  Multiplexer #(.Bits(32)) multiplexer_3 (
    .sel(enter_excep), .in_0(demultiplexer_2_out_5), .in_1(mcause_data), .out(mcause_in));
  Multiplexer #(.Bits(32)) multiplexer_4 (
    .sel(enter_excep), .in_0(demultiplexer_2_out_6), .in_1(PC_ip), .out(mtval_in));
  assign {and_2_out[31:12], int_peripheral, and_2_out[10:8], int_timer, and_2_out[6:4], int_soft, and_2_out[2:0]} = mip_out & mip_out;  // And and_2, 32 bits wide
  Multiplexer #(.Bits(32)) multiplexer_5 (
    .sel(mret), .in_0(multiplexer_1_out),
    .in_1({mstatus_out[31:8], 1'b1, mstatus_out[6:4], mstatus_out[7], mstatus_out[2:0]}), .out(mstatus_in));
  Register #(.Bits(32)) mepc (.D(mepc_in), .C(Clock), .en(mepc_en), .Q(mepc_out_t));
  or or_2 (or_2_out, int_soft, int_timer, int_peripheral);
  not not_1 (EN_excep, Exception_code[0]);
  assign Addr_jmp = mret ? mepc_out_t : 32'bz;  // Driver driver_3
  Demultiplexer #(.Selector_Bits(3)) demultiplexer_3 (
    .sel(csr_addr_spliter_1_lut_out), .in(WE_CSR), .out_0(demultiplexer_3_out_0),
    .out_1(demultiplexer_3_out_1), .out_2(mie_en), .out_3(mtvec_en), .out_4(demultiplexer_3_out_4),
    .out_5(demultiplexer_3_out_5), .out_6(demultiplexer_3_out_6));  // open: out_7
  PullDown #(.Bits(32)) pulldown_1 (.out(Addr_jmp));
  and and_3 (and_3_out, or_2_out, EN_ie);
  or or_3 (or_3_out, mret, enter_excep);
  or or_4 (or_4_out, EN_excep, and_3_out);
  and and_4 (Do_intperipheral, ~EN_excep, EN_ie, int_peripheral);  // And
  Multiplexer multiplexer_6 (.sel(or_3_out), .in_0(demultiplexer_3_out_1), .in_1(1'b1), .out(mstatus_en));
  Multiplexer multiplexer_7 (.sel(enter_excep), .in_0(demultiplexer_3_out_4), .in_1(1'b1), .out(mepc_en));
  Multiplexer multiplexer_8 (.sel(enter_excep), .in_0(demultiplexer_3_out_5), .in_1(1'b1), .out(mcause_en));
  Multiplexer multiplexer_9 (.sel(enter_excep), .in_0(demultiplexer_3_out_6), .in_1(1'b1), .out(mtval));
  and and_5 (enter_excep, or_4_out, ~mret);  // And
  and and_6 (Do_intsoft, ~EN_excep, ~Do_intperipheral, EN_ie, int_soft);  // And
  and and_7 (and_7_out, ~mtvec_out[0], enter_excep);  // And
  RegisterFile #(.AddrBits(12), .Bits(32)) CSR_Registers (
    .Din(demultiplexer_2_out_0), .we(demultiplexer_3_out_0), .Rw(demultiplexer_1_out_0), .C(Clock),
    .Ra(Addr_csr1), .Rb(Addr_csr2), .Da(CSR_Registers_da), .Db(CSR_Registers_db));
  csr_addr_spliter csr_addr_spliter_2 (.Addr_csr(Addr_csr1), .LUT_out(csr_addr_spliter_2_lut_out));
  csr_addr_spliter csr_addr_spliter_3 (.Addr_csr(Addr_csr2), .LUT_out(csr_addr_spliter_3_lut_out));
  and and_8 (and_8_out, EN_excep, enter_excep);
  and and_9 (Do_inttimer, ~EN_excep, ~Do_intsoft, ~Do_intperipheral, EN_ie, int_timer);  // And
  Add #(.Bits(32)) add_1 (.a({mtvec_out[31:2], 2'b00}), .b(offset_jmp), .c_i(1'b0), .s(vec_offset));  // open: c_o
  or or_5 (or_5_out, EN_excep, and_7_out);
  assign mcause_data = and_8_out ? {1'b0, Exception_code[31:1]} : 32'bz;  // Driver driver_4
  and and_10 (and_10_out, or_5_out, ~mret);  // And
  assign Addr_jmp = and_10_out ? {mtvec_out[31:2], 2'b00} : 32'bz;  // Driver driver_5
  and and_11 (and_11_out, Do_intsoft, mtvec_out[0], ~mret);  // And
  and and_12 (and_12_out, Do_inttimer, mtvec_out[0], ~mret);  // And
  and and_13 (and_13_out, Do_intperipheral, mtvec_out[0], ~mret);  // And
  assign Addr_jmp = and_11_out ? vec_offset : 32'bz;  // Driver driver_6
  assign Addr_jmp = and_13_out ? vec_offset : 32'bz;  // Driver driver_7
  Multiplexer #(.Selector_Bits(3), .Bits(32)) multiplexer_10 (
    .sel(csr_addr_spliter_2_lut_out), .in_0(CSR_Registers_da),
    .in_1({mstatus_out[31:4], EN_ie, mstatus_out[2:0]}), .in_2(mie_out), .in_3(mtvec_out), .in_4(mepc_out_t),
    .in_5(mcause_out), .in_6(mtval_out), .in_7(mip_out), .out(Out_csr1));
  Multiplexer #(.Selector_Bits(3), .Bits(32)) multiplexer_11 (
    .sel(csr_addr_spliter_3_lut_out), .in_0(CSR_Registers_db),
    .in_1({mstatus_out[31:4], EN_ie, mstatus_out[2:0]}), .in_2(mie_out), .in_3(mtvec_out), .in_4(mepc_out_t),
    .in_5(mcause_out), .in_6(mtval_out), .in_7(mip_out), .out(Out_csr2));
  and and_14 (and_14_out, EN_excep, enter_excep);
  Register #(.Bits(32)) pc_reg (.D(PC_Addr), .C(Clock), .en(1'b1), .Q(pc_reg_q));
  assign Addr_jmp = and_12_out ? vec_offset : 32'bz;  // Driver driver_8
  assign mepc_data = and_14_out ? pc_reg_q : 32'bz;  // Driver driver_9
  assign offset_jmp = and_11_out ? 32'hc : 32'bz;  // Driver driver_10
  assign offset_jmp = and_13_out ? 32'h2c : 32'bz;  // Driver driver_11
  assign offset_jmp = and_12_out ? 32'h1c : 32'bz;  // Driver driver_12
  not not_2 (not_2_out, EN_excep);
  and and_15 (and_15_out, not_2_out, enter_excep);
  LookUpTable #(.Bits(31)) lookuptable_1 (
    .in0(int_soft), .in1(int_timer), .in2(int_peripheral), .out(lookuptable_1_out));
  assign mcause_data = and_15_out ? {1'b1, lookuptable_1_out} : 32'bz;  // Driver driver_13
  Register #(.Bits(32)) pcnext_reg (.D(PC_next), .C(Clock), .en(1'b1), .Q(pcnext_reg_q));
  and and_16 (and_16_out, not_2_out, enter_excep);
  Add #(.Bits(32)) add_2 (.a(mepc_out), .b(32'h1), .c_i(1'b0), .s(add_2_s));  // open: c_o
  assign mepc_data = and_16_out ? pcnext_reg_q : 32'bz;  // Driver driver_14
  Register #(.Bits(32)) register_1 (.D(add_2_s), .C(Clock), .en(enter_excep), .Q(mepc_out));

  assign ecode_out = Exception_code;
  assign timer_en = mret;

  // Other names for the same wires on the sheet: c = Clock; mstatus_out[3] = EN_ie; vec_mode = mtvec_out[0];
  //   vec_base[31:2] = mtvec_out[31:2]

  // Notes on the sheet:
  //   contents of lookuptable_1 (hex, n*v repeats v):
  //   0,3,7,0,b
endmodule
