// Digital circuit main.dig as structural Verilog
module main (
  input  Clock,
  input  GPIO_in1,
  input  GPIO_in2,
  input  GPIO_in3,
  input  GPIO_in4,
  input  GPIO_in5,
  input  GPIO_in6,
  input  GPIO_in7,
  input  GPIO_in8,
  input  GPIO_in9,
  input  GPIO_in10,
  output GPIO_1,
  output GPIO_2,
  output GPIO_3,
  output GPIO_4,
  output GPIO_5,
  output GPIO_6,
  output GPIO_7,
  output GPIO_8,
  output GPIO_9,
  output GPIO_10
);

  wire and_1_out, and_2_out, ard_en, c, crd_en, cust_ctrl_1_pc_init, Cust_op, int_peripheral, jrd_en, lrd_en,
       man_out, memgpio_en, or_1_out, or_2_out, PC_except, PC_jmp, We_mem, which_memory_1_oe_ker,
       which_memory_1_oe_ssd;
  wire [3:0] storebytes_size;
  wire [4:0] driver_9_out, instruction_decoder_1_rs1, instruction_decoder_1_rs2, rd;
  wire [5:0] instruction_decoder_1_csr_op;
  wire [6:0] imm_7;
  wire [7:0] instruction_decoder_1_machine_op, rom_1_d;
  wire [8:0] instruction_decoder_1_jmp_op, instruction_decoder_1_mem_op;
  wire [11:0] imm_12;
  wire [18:0] instruction_decoder_1_alu_op;
  wire [19:0] imm_20;
  wire [23:0] which_memory_1_ssd_addr;
  wire [31:0] Addr_except, Addr_jmp, alu_1_rd_out, csr_1_rd_out, data_mem, data_memgpio, debug_data,
       driver_1_out, driver_3_out, driver_5_out, instruction_code, instuction_jump_unit_1_rd_out,
       int_gpiocode, Invalid_op, mem_addr, memory_1_data_out, memory_operation_unit_1_rd_out, Out_csr1,
       PC_exec, PC_next, rs1_data, rs2_data;

  and and_1 (and_1_out, PC_jmp, ~PC_except);  // And
  or or_1 (or_1_out, PC_jmp, PC_except);
  PullDown pulldown_1 (.out(PC_except));
  assign driver_1_out = and_1_out ? Addr_jmp : 32'bz;  // Driver driver_1
  assign driver_1_out = PC_except ? Addr_except : 32'bz;  // Driver driver_2
  PullDown #(.Bits(32)) pulldown_2 (.out(Addr_except));
  PullDown pulldown_3 (.out(int_peripheral));
  cust_ctrl cust_ctrl_1 (.op_code(instruction_code), .cust_code(Cust_op), .Clock(c), .PC_init(cust_ctrl_1_pc_init));
  gpio u_gpio_1 (
    .Clock(c), .Addr_w(mem_addr), .Data_in(data_mem), .we(We_mem), .Addr_rd(mem_addr),
    .int_gate(int_peripheral), .GPIO1_in(GPIO_in1), .GPIO2_in(GPIO_in2), .GPIO3_in(GPIO_in3),
    .GPIO4_in(GPIO_in4), .GPIO5_in(GPIO_in5), .GPIO6_in(GPIO_in6), .GPIO7_in(GPIO_in7), .GPIO8_in(GPIO_in8),
    .GPIO9_in(GPIO_in9), .GPIO10_in(GPIO_in10), .Out_rd(data_memgpio), .Out_en(memgpio_en),
    .perint_code(int_gpiocode), .GPIO1_out(GPIO_1), .GPIO2_out(GPIO_2), .GPIO3_out(GPIO_3),
    .GPIO4_out(GPIO_4), .GPIO5_out(GPIO_5), .GPIO6_out(GPIO_6), .GPIO7_out(GPIO_7), .GPIO8_out(GPIO_8),
    .GPIO9_out(GPIO_9), .GPIO10_out(GPIO_10));
  program_counter program_counter_1 (
    .PC_inited(cust_ctrl_1_pc_init), .En(1'b1), .Clock(c), .Addr_jmp(driver_1_out), .En_jmp(or_1_out),
    .PC_next(PC_next), .PC_exec(PC_exec));
  debug debug_1 (.EN(1'b0), .C_in(Clock), .man(man_out), .PC_cur(PC_exec), .clock(c));
  Button man (.out(man_out));
  which_memory which_memory_1 (
    .mem_addr(mem_addr), .Oe_ker(which_memory_1_oe_ker), .OE_ssd(which_memory_1_oe_ssd),
    .SSD_addr(which_memory_1_ssd_addr));
  and and_2 (and_2_out, PC_exec[25], ~PC_exec[31]);  // And
  memory memory_1 (
    .OE_PC(and_2_out), .Addr_PC(PC_exec), .WE(We_mem), .Addr(mem_addr), .Data_in(data_mem),
    .ByteSize_in(storebytes_size), .Clock(c), .DataPC_out(instruction_code), .Data_out(memory_1_data_out));
  ROM #(.AddrBits(24), .Bits(8)) rom_1 (.A(which_memory_1_ssd_addr), .sel(1'b1), .D(rom_1_d));
  boot_rom boot_rom_1 (.Addr(PC_exec[23:0]), .En(PC_exec[31]), .Out_code(instruction_code));
  assign driver_3_out = which_memory_1_oe_ker ? memory_1_data_out : 32'bz;  // Driver driver_3
  assign driver_3_out = which_memory_1_oe_ssd ? {{24{1'b0}}, rom_1_d} : 32'bz;  // Driver driver_4
  instruction_decoder instruction_decoder_1 (
    .Instruction_In(instruction_code), .EN(1'b1), .rd(rd), .rs1(instruction_decoder_1_rs1),
    .rs2(instruction_decoder_1_rs2), .imm_2531(imm_7), .imm_1231(imm_20), .imm_2032(imm_12),
    .invalid(Invalid_op), .csr_op(instruction_decoder_1_csr_op), .jmp_op(instruction_decoder_1_jmp_op),
    .alu_op(instruction_decoder_1_alu_op), .mem_op(instruction_decoder_1_mem_op),
    .machine_op(instruction_decoder_1_machine_op), .cust_op(Cust_op));
  memory_operation_unit memory_operation_unit_1 (
    .MemOp_in(instruction_decoder_1_mem_op), .Data_in(driver_3_out), .rs1(rs1_data), .rs2(rs2_data),
    .Offset_12(imm_12), .Offset_7(imm_7), .Offset_5(rd), .imm_20(imm_20), .rEN_out(lrd_en),
    .rd_out(memory_operation_unit_1_rd_out), .mwe_out(We_mem), .Addr_out(mem_addr), .Mem_out(data_mem),
    .StoreByteSize_out(storebytes_size));
  csr csr_1 (
    .CSRCode_in(instruction_decoder_1_csr_op), .Data_in(rs1_data), .Csr_Addr(imm_12),
    .Imm5_in(instruction_decoder_1_rs1), .Data_temp(Out_csr1), .Clock(c), .En(crd_en), .rd_out(csr_1_rd_out));  // open: Out_csr, Addr_csr
  PullDown #(.Bits(32)) pulldown_4 (.out(Out_csr1));
  mechine_op_unit mechine_op_unit_1 (.mechine_op(instruction_decoder_1_machine_op));  // open: mret
  instuction_jump_unit instuction_jump_unit_1 (
    .jmp_op(instruction_decoder_1_jmp_op), .PC_cur(PC_exec), .rs1_in(rs1_data), .rs2_in(rs2_data),
    .Imm12_in(imm_12), .Imm20_in(imm_20), .Imm7_in(imm_7), .offset_5(rd), .EN_out(jrd_en),
    .rd_out(instuction_jump_unit_1_rd_out), .Addr_jmp(Addr_jmp), .En_jmp(PC_jmp));
  alu alu_1 (
    .Alu_in(instruction_decoder_1_alu_op), .rs1_in(rs1_data), .rs2_in(rs2_data), .Imm12_in(imm_12),
    .EN_out(ard_en), .rd_out(alu_1_rd_out), .InvalidOP_out(Invalid_op));
  or or_2 (or_2_out, crd_en, jrd_en, ard_en, lrd_en);
  assign driver_5_out = crd_en ? csr_1_rd_out : 32'bz;  // Driver driver_5
  assign driver_5_out = jrd_en ? instuction_jump_unit_1_rd_out : 32'bz;  // Driver driver_6
  assign driver_5_out = ard_en ? alu_1_rd_out : 32'bz;  // Driver driver_7
  assign driver_5_out = lrd_en ? memory_operation_unit_1_rd_out : 32'bz;  // Driver driver_8
  assign driver_9_out = or_2_out ? rd : 5'bz;  // Driver driver_9
  PullDown #(.Bits(5)) pulldown_5 (.out(driver_9_out));
  reg_file_riscv reg_file_riscv_1 (
    .WE(driver_9_out), .OE_P1(instruction_decoder_1_rs1), .OE_P2(instruction_decoder_1_rs2),
    .OE_P3(5'b01110), .Din(driver_5_out), .Clock(c), .Output_P1(rs1_data), .Output_P2(rs2_data),
    .Output_P3(debug_data));

  // Other names for the same wires on the sheet: gpio_out1 = GPIO_1; gpio_out2 = GPIO_2; gpio_out3 = GPIO_3;
  //   gpio_out4 = GPIO_4; gpio_out5 = GPIO_5; gpio_out6 = GPIO_6; gpio_out7 = GPIO_7; gpio_out8 = GPIO_8;
  //   gpio_out9 = GPIO_9; gpio_out10 = GPIO_10

  // Notes on the sheet:
  //   Clock: Hz: 5000
  //   Peripheral GPIO
  //   contents of rom_1 (hex, n*v repeats v):
  //   37,1,0,1,ef,0,40,0,13,1,1,ff,13,5,10,0,23,26,11,0,ef,0,0,5,13
  //   ,5,10,0,ef,0,40,9,13,5,80,3e,ef,0,0,c,13,5,0,0,ef,0,40,8,13,5
  //   ,80,3e,ef,0,0,b,13,5,10,0,ef,0,40,7,6f,f0,1f,fe,63,8e,5,0,b7,7
  //   ,0,a0,3,a7,7,0,13,5,f5,ff,b3,95,a5,0,b3,e5,e5,0,23,a0,b7,0,67
  //   ,80,0,0,b7,7,0,a0,23,a0,a7,0,67,80,0,0,37,7,0,a0,13,5,f5,ff,93
  //   ,7,10,0,13,7,47,0,3,27,7,0,b3,97,a7,0,63,8a,5,0,33,67,f7,0,b7
  //   ,7,0,a0,23,a2,e7,0,67,80,0,0,93,c7,f7,ff,33,f7,e7,0,b7,7,0,a0
  //   ,23,a2,e7,0,67,80,0,0,b7,7,0,a0,23,a2,a7,0,67,80,0,0,b7,7,0,a0
  //   ,3,a5,47,0,67,80,0,0,b7,7,0,a0,83,a6,47,0,13,7,f5,ff,93,7,10,0
  //   ,b3,97,e7,0,33,f5,d7,0,67,80,0,0,13,1,1,ff,13,55,15,0,23,26,a1
  //   ,0,83,27,c1,0,13,87,f7,ff,23,26,e1,0,63,8c,7,0,13,0,0,0,83,27
  //   ,c1,0,13,87,f7,ff,23,26,e1,0,e3,98,7,fe,13,1,1,1,67,80
endmodule
