// Digital circuit main3.dig as structural Verilog
module main3 (
);

  inst_decoder #(.applicationType("IVERILOG"), .iverilogOptions("-I /Users/markren/LocalFiles/myRISCV/netlist/verilog/src -I /Users/markren/LocalFiles/myRISCV/netlist/verilog/src/core -I /Users/markren/LocalFiles/myRISCV/netlist/verilog/src/core/peripherals"), .CodeFile("/Users/markren/LocalFiles/myRISCV/netlist/verilog/src/core/inst_decoder.v")) u_inst_decoder ();  // open: instruction_code, en, rd, rs1, rs2, imm_1231, invalid_instruction, inst_flags
  ex_alu #(.applicationType("IVERILOG"), .iverilogOptions("-I /Users/markren/LocalFiles/myRISCV/netlist/verilog/src -I /Users/markren/LocalFiles/myRISCV/netlist/verilog/src/core -I /Users/markren/LocalFiles/myRISCV/netlist/verilog/src/core/peripherals"), .CodeFile("/Users/markren/LocalFiles/myRISCV/netlist/verilog/src/core/ex_alu.v")) u_ex_alu ();  // open: rst, rd, rs1_data, rs2_data, imm_1231, inst_flags, rd_out, out_en, rd_data
  ex_csr #(.applicationType("IVERILOG"), .iverilogOptions("-I /Users/markren/LocalFiles/myRISCV/netlist/verilog/src -I /Users/markren/LocalFiles/myRISCV/netlist/verilog/src/core -I /Users/markren/LocalFiles/myRISCV/netlist/verilog/src/core/peripherals"), .CodeFile("/Users/markren/LocalFiles/myRISCV/netlist/verilog/src/core/ex_csr.v")) u_ex_csr ();  // open: rst, rd, imm_1519, rs1_data, csr_data, imm_2031, inst_flags, rd_out, out_en, rd_data, csr_out_en, csrw_data, csrw_addr
  ex_mem #(.applicationType("IVERILOG"), .iverilogOptions("-I /Users/markren/LocalFiles/myRISCV/netlist/verilog/src -I /Users/markren/LocalFiles/myRISCV/netlist/verilog/src/core -I /Users/markren/LocalFiles/myRISCV/netlist/verilog/src/core/peripherals"), .CodeFile("/Users/markren/LocalFiles/myRISCV/netlist/verilog/src/core/ex_mem.v")) u_ex_mem ();  // open: clk, rst, rd, rs1_data, rs2_data, imm_2031, pc, mem_data_in, mem_read_ready, mem_write_ready, inst_flags, wb_rd_wait, rd_out, rd_en, rd_data, byte_size, mem_data, mem_addr, busy_flag, mem_write_en, mem_read_en
  registers #(.applicationType("IVERILOG"), .iverilogOptions("-I /Users/markren/LocalFiles/myRISCV/netlist/verilog/src -I /Users/markren/LocalFiles/myRISCV/netlist/verilog/src/core -I /Users/markren/LocalFiles/myRISCV/netlist/verilog/src/core/peripherals"), .CodeFile("/Users/markren/LocalFiles/myRISCV/netlist/verilog/src/core/registers.v")) u_registers ();  // open: clk, rst, rs1_addr, rs2_addr, rd_addr, rd_data, rd_en, rs1_out, rs2_out
  ex_branch #(.applicationType("IVERILOG"), .iverilogOptions("-I /Users/markren/LocalFiles/myRISCV/netlist/verilog/src -I /Users/markren/LocalFiles/myRISCV/netlist/verilog/src/core -I /Users/markren/LocalFiles/myRISCV/netlist/verilog/src/core/peripherals"), .CodeFile("/Users/markren/LocalFiles/myRISCV/netlist/verilog/src/core/ex_branch.v")) u_ex_branch ();  // open: rst, pc_cur, pc_next, rd, rs1_data, rs2_data, imm_1231, inst_flags, branch_hazard, pc_next_out, jmp_en, rd_out, rd_data_out, b_n_jmp, rd_out_en
  registers_csr #(.applicationType("IVERILOG"), .iverilogOptions("-I /Users/markren/LocalFiles/myRISCV/netlist/verilog/src -I /Users/markren/LocalFiles/myRISCV/netlist/verilog/src/core -I /Users/markren/LocalFiles/myRISCV/netlist/verilog/src/core/peripherals"), .CodeFile("/Users/markren/LocalFiles/myRISCV/netlist/verilog/src/core/registers_csr.v")) u_registers_csr ();  // open: clk, rst, exp_pc, exp_pc_next, exp_val, exception_code, exception_en, int_jmp_ready, mret_en, peripheral_int_code, soft_int_code, clk_timer, mtimecmp_low, mtimecmp_high, set_mtimecmp_low, set_mtimecmp_high, csr_read_addr, csrw_addr, w_data, write_en, int_en, jmp_en, jmp_pc, cur_int_code, mtime_low, mtime_high, csr_out
endmodule
