// Digital circuit mechine_op_unit.dig as structural Verilog
module mechine_op_unit (
  input  [7:0] machine_op,
  output mret
);


  assign mret = machine_op[2];

  // Other names for the same wires on the sheet: ebreak = machine_op[0]; ecall = machine_op[1];
  //   sfence_vma = machine_op[3]; sret = machine_op[4]; wfi = machine_op[5]; fence = machine_op[6];
  //   fence_i = machine_op[7]
endmodule
