// Digital circuit memory.dig as structural Verilog
module memory (
  input  OE_PC,
  input  [31:0] Addr_PC,
  input  WE,
  input  [31:0] Addr,
  input  [31:0] Data_in,
  input  [3:0] ByteSize_in,
  input  Clock,
  output [31:0] DataPC_out,
  output [31:0] Data_out
);

  wire we0, we1, we2, we3;
  wire [3:0] Rotate_left_2_out4;
  wire [7:0] Rotate_left_out32, Rotate_left_out32_2, Rotate_left_out32_3, Rotate_left_out32_4, x00_d1,
       x00_d2, x01_d1, x01_d2, x10_d1, x10_d2, x11_d1, x11_d2;
  wire [31:0] Rotate_right_2_out32;

  barrel_shifter8 Rotate_left (
    .shift_byte(Addr[1:0]), .in32(Data_in), .Direction(1'b0), .mode(2'b00),
    .out32({Rotate_left_out32_4, Rotate_left_out32_3, Rotate_left_out32_2, Rotate_left_out32}));
  barrel_shifter1 Rotate_left_2 (
    .shift(Addr[1:0]), .in4(ByteSize_in), .Direction(1'b0), .mode(2'b00), .out4(Rotate_left_2_out4));
  PullDown pulldown_1 (.out(WE));
  Multiplexer #(.Bits(4)) multiplexer_1 (
    .sel(WE), .in_0(4'b0000), .in_1(Rotate_left_2_out4), .out({we3, we2, we1, we0}));
  RAMDualAccess #(.AddrBits(24), .Bits(8)) x00 (
    .str(we0), .C(Clock), .ld(1'b1), .A1(Addr[25:2]), .Din1(Rotate_left_out32), .A2(Addr_PC[25:2]),
    .D1(x00_d1), .D2(x00_d2));
  RAMDualAccess #(.AddrBits(24), .Bits(8)) x01 (
    .str(we1), .C(Clock), .ld(1'b1), .A1(Addr[25:2]), .Din1(Rotate_left_out32_2), .A2(Addr_PC[25:2]),
    .D1(x01_d1), .D2(x01_d2));
  RAMDualAccess #(.AddrBits(24), .Bits(8)) x10 (
    .str(we2), .C(Clock), .ld(1'b1), .A1(Addr[25:2]), .Din1(Rotate_left_out32_3), .A2(Addr_PC[25:2]),
    .D1(x10_d1), .D2(x10_d2));
  RAMDualAccess #(.AddrBits(24), .Bits(8)) x11 (
    .str(we3), .C(Clock), .ld(1'b1), .A1(Addr[25:2]), .Din1(Rotate_left_out32_4), .A2(Addr_PC[25:2]),
    .D1(x11_d1), .D2(x11_d2));
  barrel_shifter8 Rotate_right (
    .shift_byte(Addr[1:0]), .in32({x11_d1, x10_d1, x01_d1, x00_d1}), .Direction(1'b1), .mode(2'b00),
    .out32(Data_out));
  barrel_shifter8 Rotate_right_2 (
    .shift_byte(Addr_PC[1:0]), .in32({x11_d2, x10_d2, x01_d2, x00_d2}), .Direction(1'b1), .mode(2'b00),
    .out32(Rotate_right_2_out32));
  assign DataPC_out = OE_PC ? Rotate_right_2_out32 : 32'bz;  // Driver driver_1

  // Other names for the same wires on the sheet: shift[1:0] = Addr[1:0]; shift_PC[1:0] = Addr_PC[1:0]; c = Clock
endmodule
