// Digital circuit memory_operation_unit.dig as structural Verilog
module memory_operation_unit (
  input  [8:0] MemOp_in,
  input  [31:0] Data_in,
  input  [31:0] rs1,
  input  [31:0] rs2,
  input  [11:0] Offset_12,
  input  [6:0] Offset_7,
  input  [4:0] Offset_5,
  input  [19:0] imm_20,
  output rEN_out,
  output [31:0] rd_out,
  output mwe_out,
  output [31:0] Addr_out,
  output [31:0] Mem_out,
  output [3:0] StoreByteSize_out
);

  wire decoder_1_out_0, decoder_1_out_1, decoder_1_out_2, decoder_1_out_3, decoder_1_out_4, decoder_1_out_5,
       decoder_1_out_6, decoder_1_out_7, decoder_1_out_8, priorityencoder_1_any;
  wire [1:0] or_1_out;
  wire [3:0] multiplexer_3_out, priorityencoder_1_num, pulldown_3_out, pulldown_4_out;
  wire [31:0] bitextender_1_out, bitextender_2_out, bitextender_3_out, bitextender_4_out, multiplexer_1_out,
       multiplexer_6_out, pulldown_1_out, pulldown_2_out, pulldown_5_out;

  PriorityEncoder #(.Selector_Bits(4)) priorityencoder_1 (
    .in0(MemOp_in[0]), .in1(MemOp_in[1]), .in2(MemOp_in[2]), .in3(MemOp_in[3]), .in4(MemOp_in[4]),
    .in5(MemOp_in[5]), .in6(MemOp_in[6]), .in7(MemOp_in[7]), .in8(MemOp_in[8]), .in9(1'b0), .in10(1'b0),
    .in11(1'b0), .in12(1'b0), .in13(1'b0), .in14(1'b0), .in15(1'b0), .num(priorityencoder_1_num),
    .any(priorityencoder_1_any));
  BitExtender #(.outputBits(32)) bitextender_1 (.in(Data_in[7:0]), .out(bitextender_1_out));
  BitExtender #(.inputBits(16), .outputBits(32)) bitextender_2 (.in(Data_in[15:0]), .out(bitextender_2_out));
  Multiplexer #(.Selector_Bits(4), .Bits(32)) multiplexer_1 (
    .sel(priorityencoder_1_num), .in_0({imm_20, {12{1'b0}}}), .in_1(bitextender_1_out),
    .in_2(bitextender_2_out), .in_3(Data_in), .in_4({{24{1'b0}}, Data_in[7:0]}),
    .in_5({{16{1'b0}}, Data_in[15:0]}), .in_6(pulldown_1_out), .in_7(pulldown_1_out), .in_8(pulldown_1_out),
    .in_9(pulldown_1_out), .in_10(pulldown_1_out), .in_11(pulldown_1_out), .in_12(pulldown_1_out),
    .in_13(pulldown_1_out), .in_14(pulldown_1_out), .in_15(pulldown_1_out), .out(multiplexer_1_out));
  PullDown #(.Bits(32)) pulldown_1 (.out(pulldown_1_out));
  Decoder #(.Selector_Bits(4)) decoder_1 (
    .sel(priorityencoder_1_num), .out_0(decoder_1_out_0), .out_1(decoder_1_out_1), .out_2(decoder_1_out_2),
    .out_3(decoder_1_out_3), .out_4(decoder_1_out_4), .out_5(decoder_1_out_5), .out_6(decoder_1_out_6),
    .out_7(decoder_1_out_7), .out_8(decoder_1_out_8));  // open: out_9, out_10, out_11, out_12, out_13, out_14, out_15
  Multiplexer #(.Bits(32)) multiplexer_2 (
    .sel(priorityencoder_1_any), .in_0(pulldown_2_out), .in_1(multiplexer_1_out), .out(rd_out));
  PullDown #(.Bits(32)) pulldown_2 (.out(pulldown_2_out));
  or or_1 (or_1_out[0], decoder_1_out_0, decoder_1_out_1, decoder_1_out_2, decoder_1_out_3, decoder_1_out_4, decoder_1_out_5);
  or or_2 (or_1_out[1], decoder_1_out_6, decoder_1_out_7, decoder_1_out_8);
  Multiplexer #(.Selector_Bits(4), .Bits(4)) multiplexer_3 (
    .sel(priorityencoder_1_num), .in_0(4'b0000), .in_1(4'b0001), .in_2(4'b0011), .in_3(4'b1111),
    .in_4(4'b0001), .in_5(4'b0011), .in_6(4'b0001), .in_7(4'b0011), .in_8(4'b1111), .in_9(pulldown_3_out),
    .in_10(pulldown_3_out), .in_11(pulldown_3_out), .in_12(pulldown_3_out), .in_13(pulldown_3_out),
    .in_14(pulldown_3_out), .in_15(pulldown_3_out), .out(multiplexer_3_out));
  PullDown #(.Bits(4)) pulldown_3 (.out(pulldown_3_out));
  Multiplexer #(.Bits(2)) multiplexer_4 (
    .sel(priorityencoder_1_any), .in_0(2'b00), .in_1(or_1_out), .out({mwe_out, rEN_out}));
  PullDown #(.Bits(4)) pulldown_4 (.out(pulldown_4_out));
  Multiplexer #(.Bits(4)) multiplexer_5 (
    .sel(priorityencoder_1_any), .in_0(pulldown_4_out), .in_1(multiplexer_3_out), .out(StoreByteSize_out));
  BitExtender #(.inputBits(12), .outputBits(32)) bitextender_3 (.in(Offset_12), .out(bitextender_3_out));
  BitExtender #(.inputBits(12), .outputBits(32)) bitextender_4 (.in({Offset_7, Offset_5}), .out(bitextender_4_out));
  Multiplexer #(.Selector_Bits(4), .Bits(32)) multiplexer_6 (
    .sel(priorityencoder_1_num), .in_0(pulldown_5_out), .in_1(bitextender_3_out), .in_2(bitextender_3_out),
    .in_3(bitextender_3_out), .in_4({{20{1'b0}}, Offset_12}), .in_5({{20{1'b0}}, Offset_12}),
    .in_6(bitextender_4_out), .in_7(bitextender_4_out), .in_8(bitextender_4_out), .in_9(pulldown_5_out),
    .in_10(pulldown_5_out), .in_11(pulldown_5_out), .in_12(pulldown_5_out), .in_13(pulldown_5_out),
    .in_14(pulldown_5_out), .in_15(pulldown_5_out), .out(multiplexer_6_out));
  PullDown #(.Bits(32)) pulldown_5 (.out(pulldown_5_out));
  Add #(.Bits(32)) add_1 (.a(rs1), .b(multiplexer_6_out), .c_i(1'b0), .s(Addr_out));  // open: c_o

  assign Mem_out = rs2;

  // Other names for the same wires on the sheet: b[7:0] = Data_in[7:0]; h[15:0] = Data_in[15:0]; w[31:0] = Data_in;
  //   lui = MemOp_in[0]; lb = MemOp_in[1]; lh = MemOp_in[2]; lw = MemOp_in[3]; lbu = MemOp_in[4]; lhu = MemOp_in[5];
  //   sb = MemOp_in[6]; sh = MemOp_in[7]; sw = MemOp_in[8]

  // Notes on the sheet:
  //   rEN_out: register write enable
  //   mwe_out: memory write enable
endmodule
