// Digital circuit program_counter.dig as structural Verilog
module program_counter (
  input  PC_inited,
  input  En,
  input  Clock,
  input  [31:0] Addr_jmp,
  input  En_jmp,
  output [31:0] PC_next,
  output [31:0] PC_exec
);

  wire and_1_out;
  wire [31:0] add_1_s, multiplexer_1_out, PC_reg_q;

  Multiplexer #(.Bits(32)) multiplexer_1 (
    .sel(PC_inited), .in_0(32'h80000000), .in_1(PC_exec), .out(multiplexer_1_out));
  Add #(.Bits(32)) add_1 (.a(multiplexer_1_out), .b(32'h4), .c_i(1'b0), .s(add_1_s));  // open: c_o
  and and_1 (and_1_out, En, En_jmp);
  Multiplexer #(.Bits(32)) multiplexer_2 (.sel(and_1_out), .in_0(add_1_s), .in_1(Addr_jmp), .out(PC_next));
  Register #(.Bits(32)) PC_reg (.D(PC_next), .C(Clock), .en(En), .Q(PC_reg_q));
  Multiplexer #(.Bits(32)) multiplexer_3 (.sel(PC_inited), .in_0(32'h80000000), .in_1(PC_reg_q), .out(PC_exec));

  // Other names for the same wires on the sheet: C = Clock
endmodule
