// Digital circuit reg_file_riscv.dig as structural Verilog
module reg_file_riscv (
  input  [4:0] WE,
  input  [4:0] OE_P1,
  input  [4:0] OE_P2,
  input  [4:0] OE_P3,
  input  [31:0] Din,
  input  Clock,
  output [31:0] Output_P1,
  output [31:0] Output_P2,
  output [31:0] Output_P3
);

  wire OE0, OE0_P2, OE0_P3, OE1, OE1_P2, OE1_P3, OE2, OE2_P2, OE2_P3, OE3, OE3_P2, OE3_P3, OE4, OE4_P2,
       OE4_P3, OE5, OE5_P2, OE5_P3, OE6, OE6_P2, OE6_P3, OE7, OE7_P2, OE7_P3, OE8, OE8_P2, OE8_P3, OE9,
       OE9_P2, OE9_P3, OE10, OE10_P2, OE10_P3, OE11, OE11_P2, OE11_P3, OE12, OE12_P2, OE12_P3, OE13, OE13_P2,
       OE13_P3, OE14, OE14_P2, OE14_P3, OE15, OE15_P2, OE15_P3, OE16, OE16_P2, OE16_P3, OE17, OE17_P2,
       OE17_P3, OE18, OE18_P2, OE18_P3, OE19, OE19_P2, OE19_P3, OE20, OE20_P2, OE20_P3, OE21, OE21_P2,
       OE21_P3, OE22, OE22_P2, OE22_P3, OE23, OE23_P2, OE23_P3, OE24, OE24_P2, OE24_P3, OE25, OE25_P2,
       OE25_P3, OE26, OE26_P2, OE26_P3, OE27, OE27_P2, OE27_P3, OE28, OE28_P2, OE28_P3, OE29, OE29_P2,
       OE29_P3, OE30, OE30_P2, OE30_P3, OE31, OE31_P2, OE31_P3, WE1, WE2, WE3, WE4, WE5, WE6, WE7, WE8, WE9,
       WE10, WE11, WE12, WE13, WE14, WE15, WE16, WE17, WE18, WE19, WE20, WE21, WE22, WE23, WE24, WE25, WE26,
       WE27, WE28, WE29, WE30, WE31;

  Decoder #(.Selector_Bits(5)) decoder_1 (
    .sel(OE_P3), .out_0(OE0_P3), .out_1(OE1_P3), .out_2(OE2_P3), .out_3(OE3_P3), .out_4(OE4_P3),
    .out_5(OE5_P3), .out_6(OE6_P3), .out_7(OE7_P3), .out_8(OE8_P3), .out_9(OE9_P3), .out_10(OE10_P3),
    .out_11(OE11_P3), .out_12(OE12_P3), .out_13(OE13_P3), .out_14(OE14_P3), .out_15(OE15_P3),
    .out_16(OE16_P3), .out_17(OE17_P3), .out_18(OE18_P3), .out_19(OE19_P3), .out_20(OE20_P3),
    .out_21(OE21_P3), .out_22(OE22_P3), .out_23(OE23_P3), .out_24(OE24_P3), .out_25(OE25_P3),
    .out_26(OE26_P3), .out_27(OE27_P3), .out_28(OE28_P3), .out_29(OE29_P3), .out_30(OE30_P3), .out_31(OE31_P3));
  Decoder #(.Selector_Bits(5)) decoder_2 (
    .sel(WE), .out_1(WE1), .out_2(WE2), .out_3(WE3), .out_4(WE4), .out_5(WE5), .out_6(WE6), .out_7(WE7),
    .out_8(WE8), .out_9(WE9), .out_10(WE10), .out_11(WE11), .out_12(WE12), .out_13(WE13), .out_14(WE14),
    .out_15(WE15), .out_16(WE16), .out_17(WE17), .out_18(WE18), .out_19(WE19), .out_20(WE20), .out_21(WE21),
    .out_22(WE22), .out_23(WE23), .out_24(WE24), .out_25(WE25), .out_26(WE26), .out_27(WE27), .out_28(WE28),
    .out_29(WE29), .out_30(WE30), .out_31(WE31));  // open: out_0
  PullDown #(.Bits(5)) pulldown_1 (.out(WE));
  Decoder #(.Selector_Bits(5)) decoder_3 (
    .sel(OE_P2), .out_0(OE0_P2), .out_1(OE1_P2), .out_2(OE2_P2), .out_3(OE3_P2), .out_4(OE4_P2),
    .out_5(OE5_P2), .out_6(OE6_P2), .out_7(OE7_P2), .out_8(OE8_P2), .out_9(OE9_P2), .out_10(OE10_P2),
    .out_11(OE11_P2), .out_12(OE12_P2), .out_13(OE13_P2), .out_14(OE14_P2), .out_15(OE15_P2),
    .out_16(OE16_P2), .out_17(OE17_P2), .out_18(OE18_P2), .out_19(OE19_P2), .out_20(OE20_P2),
    .out_21(OE21_P2), .out_22(OE22_P2), .out_23(OE23_P2), .out_24(OE24_P2), .out_25(OE25_P2),
    .out_26(OE26_P2), .out_27(OE27_P2), .out_28(OE28_P2), .out_29(OE29_P2), .out_30(OE30_P2), .out_31(OE31_P2));
  Decoder #(.Selector_Bits(5)) decoder_4 (
    .sel(OE_P1), .out_0(OE0), .out_1(OE1), .out_2(OE2), .out_3(OE3), .out_4(OE4), .out_5(OE5), .out_6(OE6),
    .out_7(OE7), .out_8(OE8), .out_9(OE9), .out_10(OE10), .out_11(OE11), .out_12(OE12), .out_13(OE13),
    .out_14(OE14), .out_15(OE15), .out_16(OE16), .out_17(OE17), .out_18(OE18), .out_19(OE19), .out_20(OE20),
    .out_21(OE21), .out_22(OE22), .out_23(OE23), .out_24(OE24), .out_25(OE25), .out_26(OE26), .out_27(OE27),
    .out_28(OE28), .out_29(OE29), .out_30(OE30), .out_31(OE31));
  register_32_bit register_32_bit_1 (
    .Din(Din), .Clock(Clock), .WE(WE1), .OE1(OE1), .OE2(OE1_P2), .OE3(OE1_P3), .Output1(Output_P1),
    .Output2(Output_P2), .Output3(Output_P3));  // open: data
  register_32_bit register_32_bit_2 (
    .Din(Din), .Clock(Clock), .WE(WE2), .OE1(OE2), .OE2(OE2_P2), .OE3(OE2_P3), .Output1(Output_P1),
    .Output2(Output_P2), .Output3(Output_P3));  // open: data
  register_32_bit register_32_bit_3 (
    .Din(Din), .Clock(Clock), .WE(WE3), .OE1(OE3), .OE2(OE3_P2), .OE3(OE3_P3), .Output1(Output_P1),
    .Output2(Output_P2), .Output3(Output_P3));  // open: data
  register_32_bit register_32_bit_4 (
    .Din(Din), .Clock(Clock), .WE(WE4), .OE1(OE4), .OE2(OE4_P2), .OE3(OE4_P3), .Output1(Output_P1),
    .Output2(Output_P2), .Output3(Output_P3));  // open: data
  register_32_bit register_32_bit_5 (
    .Din(Din), .Clock(Clock), .WE(WE5), .OE1(OE5), .OE2(OE5_P2), .OE3(OE5_P3), .Output1(Output_P1),
    .Output2(Output_P2), .Output3(Output_P3));  // open: data
  register_32_bit register_32_bit_6 (
    .Din(Din), .Clock(Clock), .WE(WE6), .OE1(OE6), .OE2(OE6_P2), .OE3(OE6_P3), .Output1(Output_P1),
    .Output2(Output_P2), .Output3(Output_P3));  // open: data
  register_32_bit register_32_bit_7 (
    .Din(Din), .Clock(Clock), .WE(WE7), .OE1(OE7), .OE2(OE7_P2), .OE3(OE7_P3), .Output1(Output_P1),
    .Output2(Output_P2), .Output3(Output_P3));  // open: data
  register_32_bit register_32_bit_8 (
    .Din(Din), .Clock(Clock), .WE(WE8), .OE1(OE8), .OE2(OE8_P2), .OE3(OE8_P3), .Output1(Output_P1),
    .Output2(Output_P2), .Output3(Output_P3));  // open: data
  register_32_bit register_32_bit_9 (
    .Din(Din), .Clock(Clock), .WE(WE9), .OE1(OE9), .OE2(OE9_P2), .OE3(OE9_P3), .Output1(Output_P1),
    .Output2(Output_P2), .Output3(Output_P3));  // open: data
  register_32_bit register_32_bit_10 (
    .Din(Din), .Clock(Clock), .WE(WE10), .OE1(OE10), .OE2(OE10_P2), .OE3(OE10_P3), .Output1(Output_P1),
    .Output2(Output_P2), .Output3(Output_P3));  // open: data
  register_32_bit register_32_bit_11 (
    .Din(Din), .Clock(Clock), .WE(WE11), .OE1(OE11), .OE2(OE11_P2), .OE3(OE11_P3), .Output1(Output_P1),
    .Output2(Output_P2), .Output3(Output_P3));  // open: data
  register_32_bit register_32_bit_12 (
    .Din(Din), .Clock(Clock), .WE(WE12), .OE1(OE12), .OE2(OE12_P2), .OE3(OE12_P3), .Output1(Output_P1),
    .Output2(Output_P2), .Output3(Output_P3));  // open: data
  // register_zero_32_bit register_zero_32_bit_1: pin names not known; wires that end beside it: Din, OE0, OE0_P2, OE0_P3, Output_P1, Output_P2, Output_P3
  register_32_bit register_32_bit_13 (
    .Din(Din), .Clock(Clock), .WE(WE13), .OE1(OE13), .OE2(OE13_P2), .OE3(OE13_P3), .Output1(Output_P1),
    .Output2(Output_P2), .Output3(Output_P3));  // open: data
  register_32_bit register_32_bit_14 (
    .Din(Din), .Clock(Clock), .WE(WE14), .OE1(OE14), .OE2(OE14_P2), .OE3(OE14_P3), .Output1(Output_P1),
    .Output2(Output_P2), .Output3(Output_P3));  // open: data
  register_32_bit register_32_bit_15 (
    .Din(Din), .Clock(Clock), .WE(WE15), .OE1(OE15), .OE2(OE15_P2), .OE3(OE15_P3), .Output1(Output_P1),
    .Output2(Output_P2), .Output3(Output_P3));  // open: data
  register_32_bit register_32_bit_16 (
    .Din(Din), .Clock(Clock), .WE(WE16), .OE1(OE16), .OE2(OE16_P2), .OE3(OE16_P3), .Output1(Output_P1),
    .Output2(Output_P2), .Output3(Output_P3));  // open: data
  register_32_bit register_32_bit_17 (
    .Din(Din), .Clock(Clock), .WE(WE17), .OE1(OE17), .OE2(OE17_P2), .OE3(OE17_P3), .Output1(Output_P1),
    .Output2(Output_P2), .Output3(Output_P3));  // open: data
  register_32_bit register_32_bit_18 (
    .Din(Din), .Clock(Clock), .WE(WE18), .OE1(OE18), .OE2(OE18_P2), .OE3(OE18_P3), .Output1(Output_P1),
    .Output2(Output_P2), .Output3(Output_P3));  // open: data
  register_32_bit register_32_bit_19 (
    .Din(Din), .Clock(Clock), .WE(WE19), .OE1(OE19), .OE2(OE19_P2), .OE3(OE19_P3), .Output1(Output_P1),
    .Output2(Output_P2), .Output3(Output_P3));  // open: data
  register_32_bit register_32_bit_20 (
    .Din(Din), .Clock(Clock), .WE(WE20), .OE1(OE20), .OE2(OE20_P2), .OE3(OE20_P3), .Output1(Output_P1),
    .Output2(Output_P2), .Output3(Output_P3));  // open: data
  register_32_bit register_32_bit_21 (
    .Din(Din), .Clock(Clock), .WE(WE21), .OE1(OE21), .OE2(OE21_P2), .OE3(OE21_P3), .Output1(Output_P1),
    .Output2(Output_P2), .Output3(Output_P3));  // open: data
  register_32_bit register_32_bit_22 (
    .Din(Din), .Clock(Clock), .WE(WE22), .OE1(OE22), .OE2(OE22_P2), .OE3(OE22_P3), .Output1(Output_P1),
    .Output2(Output_P2), .Output3(Output_P3));  // open: data
  register_32_bit register_32_bit_23 (
    .Din(Din), .Clock(Clock), .WE(WE23), .OE1(OE23), .OE2(OE23_P2), .OE3(OE23_P3), .Output1(Output_P1),
    .Output2(Output_P2), .Output3(Output_P3));  // open: data
  register_32_bit register_32_bit_24 (
    .Din(Din), .Clock(Clock), .WE(WE24), .OE1(OE24), .OE2(OE24_P2), .OE3(OE24_P3), .Output1(Output_P1),
    .Output2(Output_P2), .Output3(Output_P3));  // open: data
  register_32_bit register_32_bit_25 (
    .Din(Din), .Clock(Clock), .WE(WE25), .OE1(OE25), .OE2(OE25_P2), .OE3(OE25_P3), .Output1(Output_P1),
    .Output2(Output_P2), .Output3(Output_P3));  // open: data
  register_32_bit register_32_bit_26 (
    .Din(Din), .Clock(Clock), .WE(WE26), .OE1(OE26), .OE2(OE26_P2), .OE3(OE26_P3), .Output1(Output_P1),
    .Output2(Output_P2), .Output3(Output_P3));  // open: data
  register_32_bit register_32_bit_27 (
    .Din(Din), .Clock(Clock), .WE(WE27), .OE1(OE27), .OE2(OE27_P2), .OE3(OE27_P3), .Output1(Output_P1),
    .Output2(Output_P2), .Output3(Output_P3));  // open: data
  register_32_bit register_32_bit_28 (
    .Din(Din), .Clock(Clock), .WE(WE28), .OE1(OE28), .OE2(OE28_P2), .OE3(OE28_P3), .Output1(Output_P1),
    .Output2(Output_P2), .Output3(Output_P3));  // open: data
  register_32_bit register_32_bit_29 (
    .Din(Din), .Clock(Clock), .WE(WE29), .OE1(OE29), .OE2(OE29_P2), .OE3(OE29_P3), .Output1(Output_P1),
    .Output2(Output_P2), .Output3(Output_P3));  // open: data
  register_32_bit register_32_bit_30 (
    .Din(Din), .Clock(Clock), .WE(WE30), .OE1(OE30), .OE2(OE30_P2), .OE3(OE30_P3), .Output1(Output_P1),
    .Output2(Output_P2), .Output3(Output_P3));  // open: data
  register_32_bit register_32_bit_31 (
    .Din(Din), .Clock(Clock), .WE(WE31), .OE1(OE31), .OE2(OE31_P2), .OE3(OE31_P3), .Output1(Output_P1),
    .Output2(Output_P2), .Output3(Output_P3));  // open: data
endmodule
