// Digital circuit uart.dig as structural Verilog
module uart (
  input  [31:0] Addr_w,
  input  [31:0] Data_in,
  input  we,
  input  [31:0] Addr_rd,
  input  int_gate,
  input  RX,
  input  Clock,
  input  UartClock,
  output TX,
  output [31:0] Out_rd,
  output Out_en,
  output [31:0] perint_code,
  output [31:0] Data_dma,
  output [31:0] Addr_dma,
  output we_dma
);

  wire addr_compare_1_p3, addr_compare_2_p3, addr_compare_3_p3, addr_compare_4_p3, addr_compare_5_p3,
       addr_compare_6_p3, addr_compare_7_p3, and_1_out, and_2_out, and_5_out, and_6_out, comparator_1_eq,
       comparator_2_eq, comparator_2_gt, d_ff_1_q, or_1_out, or_2_out, or_3_out, pos_init, read_en,
       read_ready, save_dma, update_read, w_begin, write_able, xor_1_out;
  wire [31:0] add_1_s, buf_write_pos, uart_config;

  or or_1 (or_1_out, we_dma, pos_init);
  and and_1 (and_1_out, ~save_dma, read_ready);  // And
  PullDown pulldown_1 (.out(save_dma));
  Register #(.Bits(32)) dma_write_address (.D(buf_write_pos), .C(Clock), .en(or_1_out), .Q(Addr_dma));
  assign read_en = and_1_out ? 1'b0 : 1'bz;  // Driver driver_1
  // addr_compare addr_compare_1: pin names not known; wires that end beside it: Addr_w, 32'ha0000100, addr_compare_1_p3
  PullUp pullup_1 (.out(read_en));
  // addr_compare addr_compare_2: pin names not known; wires that end beside it: Addr_w, 32'ha0000104, addr_compare_2_p3
  // addr_compare addr_compare_3: pin names not known; wires that end beside it: Addr_w, 32'ha0000108, addr_compare_3_p3
  uart_ttl uart_ttl_1 (
    .InnerClock(UartClock), .Clock(Clock), .read_en(read_en), .Data_in(Data_in[7:0]), .write_en(w_begin),
    .RX(RX), .TX(TX), .Read_out(Data_dma[7:0]), .Read_ready(read_ready), .Writeable(write_able));
  and and_2 (and_2_out, addr_compare_1_p3, we);
  and and_3 (w_begin, addr_compare_2_p3, we);
  and and_4 (update_read, addr_compare_3_p3, we);
  Register #(.Bits(32)) u_uart_config (.D(Data_in), .C(Clock), .en(and_2_out), .Q(uart_config));
  RS_FF rs_ff_1 (.S(1'b1), .C(Clock), .R(read_ready), .nQ(save_dma));  // open: Q
  Comparator #(.Bits(32)) comparator_1 (.a(Addr_dma), .b(32'hc0000000), .eq(comparator_1_eq));  // open: gt, lt
  Comparator #(.Bits(32)) comparator_2 (
    .a(Data_in), .b(Addr_dma), .gt(comparator_2_gt), .eq(comparator_2_eq));  // open: lt
  and and_5 (and_5_out, we_dma, comparator_1_eq);
  // addr_compare addr_compare_4: pin names not known; wires that end beside it: Addr_rd, 32'ha0000100, addr_compare_4_p3
  // addr_compare addr_compare_5: pin names not known; wires that end beside it: Addr_rd, 32'ha000010c, addr_compare_5_p3
  // addr_compare addr_compare_6: pin names not known; wires that end beside it: Addr_rd, 32'ha0000110, addr_compare_6_p3
  PullDown #(.Bits(32)) pulldown_2 (.out(Addr_dma));
  or or_2 (or_2_out, comparator_2_gt, comparator_2_eq);
  // addr_compare addr_compare_7: pin names not known; wires that end beside it: {32{1'b0}}, Addr_dma, addr_compare_7_p3
  assign perint_code = and_5_out ? {32{1'b0}} : 32'bz;  // Driver driver_2
  assign Out_rd = addr_compare_4_p3 ? uart_config : 32'bz;  // Driver driver_3
  assign Out_rd = addr_compare_5_p3 ? Addr_dma : 32'bz;  // Driver driver_4
  assign Out_rd = addr_compare_6_p3 ? {{31{1'b0}}, write_able} : 32'bz;  // Driver driver_5
  and and_6 (and_6_out, update_read, or_2_out);
  assign Out_en = addr_compare_5_p3 ? 1'b1 : 1'bz;  // Driver driver_6
  assign Out_en = addr_compare_6_p3 ? 1'b1 : 1'bz;  // Driver driver_7
  D_FF d_ff_1 (.D(read_ready), .C(Clock), .Q(d_ff_1_q));  // open: nQ
  assign Out_en = addr_compare_4_p3 ? 1'b1 : 1'bz;  // Driver driver_8
  or or_3 (or_3_out, and_6_out, addr_compare_7_p3);
  xor xor_1 (xor_1_out, read_ready, d_ff_1_q);
  and and_7 (pos_init, ~read_ready, or_3_out);  // And
  assign buf_write_pos = pos_init ? 32'hc0000000 : 32'bz;  // Driver driver_9
  and and_8 (we_dma, read_ready, xor_1_out);
  Add #(.Bits(32)) add_1 (.a(Addr_dma), .b(32'h1), .c_i(1'b0), .s(add_1_s));  // open: c_o
  PullDown pulldown_3 (.out(Out_en));
  PullUp pullup_2 (.out(TX));
  assign buf_write_pos = we_dma ? add_1_s : 32'bz;  // Driver driver_10

  assign Data_dma[31:8] = {24{1'b0}};

  // Other names for the same wires on the sheet: buf_wpos[31:0] = Addr_dma; C = Clock; data_w[7:0] = Data_in[7:0];
  //   int_code[31:0] = perint_code; pos_add = we_dma; read_bit = RX; read_byte[7:0] = Data_dma[7:0]; send_bit = TX;
  //   uart_clock = UartClock

  // Notes on the sheet:
  //   Clock: Hz: 100
  //   UartClock: Hz: 50
  //   31	30   ...	6 	5 	4-1 	0
  //   writeable  readable           stop  verify  bit-size   start
endmodule
