// Digital circuit uart_ttl.dig as structural Verilog
module uart_ttl (
  input  InnerClock,
  input  Clock,
  input  read_en,
  input  [7:0] Data_in,
  input  write_en,
  input  RX,
  output TX,
  output [7:0] Read_out,
  output Read_ready,
  output Writeable
);

  wire bit_0, bit_1, bit_2, bit_3, bit_4, bit_5, bit_6, bit_7, bit_8, bit_9, bitselector_1_out,
       comparator_1_lt, comparator_2_lt, comparator_3_gt, low_clock, not_1_out, not_3_out, or_2_out,
       read_bit0, read_bit1, read_bit2, read_bit3, read_bit4, read_bit5, read_bit6, read_bit7, read_bit8,
       read_bit9, read_bit10, read_c, read_complate, read_en_t, read_real_bit, rs0, rs1, rs2, send_c,
       send_complate, ws1, ws2, ws3;
  wire [1:0] fsm_4_1_status_cur, fsm_4_2_status_cur;
  wire [3:0] bitcount_1_out, driver_7_out, read_byte_count, read_pos, send_bcount;
  wire [8:0] multiplexer_1_out, read_in, read_ret;
  wire [9:0] multiplexer_10_out, read_bytein, read_byteout;
  wire [15:0] data_write;

  PullUp pullup_1 (.out(TX));
  PullDown pulldown_1 (.out(Read_ready));
  Decoder #(.Selector_Bits(4)) decoder_1 (
    .sel(read_pos), .out_2(bit_0), .out_3(bit_1), .out_4(bit_2), .out_5(bit_3), .out_6(bit_4), .out_7(bit_5),
    .out_8(bit_6), .out_9(bit_7), .out_10(bit_8), .out_11(bit_9));  // open: out_0, out_1, out_12, out_13, out_14, out_15
  or or_1 (read_en_t, rs1, rs2);
  Counter #(.Bits(4)) counter_1 (.en(1'b1), .C(InnerClock), .clr(rs0), .out(read_pos), .ovf(read_c));
  Register #(.Bits(16)) write_reg (.D({7'b0000001, Data_in, 1'b0}), .C(Clock), .en(write_en), .Q(data_write));
  Multiplexer multiplexer_1 (.sel(bit_0), .in_0(read_ret[0]), .in_1(RX), .out(multiplexer_1_out[0]));
  Multiplexer multiplexer_2 (.sel(bit_1), .in_0(read_ret[1]), .in_1(RX), .out(multiplexer_1_out[1]));
  Multiplexer multiplexer_3 (.sel(bit_2), .in_0(read_ret[2]), .in_1(RX), .out(multiplexer_1_out[2]));
  Multiplexer multiplexer_4 (.sel(bit_3), .in_0(read_ret[3]), .in_1(RX), .out(multiplexer_1_out[3]));
  Multiplexer multiplexer_5 (.sel(bit_4), .in_0(read_ret[4]), .in_1(RX), .out(multiplexer_1_out[4]));
  Multiplexer multiplexer_6 (.sel(bit_5), .in_0(read_ret[5]), .in_1(RX), .out(multiplexer_1_out[5]));
  Multiplexer multiplexer_7 (.sel(bit_6), .in_0(read_ret[6]), .in_1(RX), .out(multiplexer_1_out[6]));
  Multiplexer multiplexer_8 (.sel(bit_7), .in_0(read_ret[7]), .in_1(RX), .out(multiplexer_1_out[7]));
  Multiplexer multiplexer_9 (.sel(bit_8), .in_0(read_ret[8]), .in_1(RX), .out(multiplexer_1_out[8]));
  Counter #(.Bits(4)) counter_2 (.en(1'b1), .C(InnerClock), .clr(Writeable), .ovf(send_c));  // open: out
  assign read_in = rs0 ? {9{1'b0}} : 9'bz;  // Driver driver_1
  FSM_4 fsm_4_1 (
    .Clock(InnerClock), .nexten_0(write_en), .nexten_1(send_complate), .nexten_2(ws2), .nexten_3(ws3),
    .direct_statusen(1'b0), .direct_status(2'b00), .falling_edge_status(4'b0000),
    .Status_cur(fsm_4_1_status_cur));
  BitSelector #(.Selector_Bits(4)) bitselector_1 (.in(data_write), .sel(send_bcount), .out(bitselector_1_out));
  assign read_bytein = rs0 ? {10{1'b0}} : 10'bz;  // Driver driver_2
  Counter #(.Bits(4)) counter_3 (.en(1'b1), .C(low_clock), .clr(rs0), .out(read_byte_count));  // open: ovf
  assign TX = ws1 ? bitselector_1_out : 1'bz;  // Driver driver_3
  or or_2 (or_2_out, send_c, send_complate);
  not not_1 (not_1_out, RX);
  assign read_in = read_en_t ? multiplexer_1_out : 9'bz;  // Driver driver_4
  Decoder #(.Selector_Bits(2)) decoder_2 (
    .sel(fsm_4_1_status_cur), .out_0(Writeable), .out_1(ws1), .out_2(ws2), .out_3(ws3));
  Counter #(.Bits(4)) counter_4 (.en(1'b1), .C(or_2_out), .clr(send_complate), .out(send_bcount));  // open: ovf
  FSM_4 fsm_4_2 (
    .Clock(InnerClock), .nexten_0(not_1_out), .nexten_1(read_complate), .nexten_2(RX), .nexten_3(read_en),
    .direct_statusen(1'b0), .direct_status(2'b00), .falling_edge_status(4'b0000),
    .Status_cur(fsm_4_2_status_cur));
  assign low_clock = rs0 ? InnerClock : 1'bz;  // Driver driver_5
  Decoder #(.Selector_Bits(4)) decoder_3 (
    .sel(read_byte_count), .out_0(read_bit0), .out_1(read_bit1), .out_2(read_bit2), .out_3(read_bit3),
    .out_4(read_bit4), .out_5(read_bit5), .out_6(read_bit6), .out_7(read_bit7), .out_8(read_bit8),
    .out_9(read_bit9), .out_10(read_bit10));  // open: out_11, out_12, out_13, out_14, out_15
  assign send_complate = ~ws1 ? 1'b0 : 1'bz;  // DriverInvSel driverinvsel_1
  Comparator #(.Bits(4)) comparator_1 (.a(read_byte_count), .b(4'b1001), .lt(comparator_1_lt));  // open: gt, eq
  Comparator #(.Bits(4)) comparator_2 (.a(send_bcount), .b(4'b1001), .lt(comparator_2_lt));  // open: gt, eq
  not not_2 (read_complate, comparator_1_lt);
  not not_3 (not_3_out, comparator_2_lt);
  Decoder #(.Selector_Bits(2)) decoder_4 (
    .sel(fsm_4_2_status_cur), .out_0(rs0), .out_1(rs1), .out_2(rs2), .out_3(Read_ready));
  assign low_clock = ~rs0 ? read_c : 1'bz;  // DriverInvSel driverinvsel_2
  assign send_complate = ws1 ? not_3_out : 1'bz;  // Driver driver_6
  Multiplexer multiplexer_10 (
    .sel(read_bit0), .in_0(read_byteout[0]), .in_1(read_real_bit), .out(multiplexer_10_out[0]));
  Multiplexer multiplexer_11 (.sel(read_bit1), .in_0(Read_out[0]), .in_1(read_real_bit), .out(multiplexer_10_out[1]));
  Multiplexer multiplexer_12 (.sel(read_bit2), .in_0(Read_out[1]), .in_1(read_real_bit), .out(multiplexer_10_out[2]));
  Multiplexer multiplexer_13 (.sel(read_bit3), .in_0(Read_out[2]), .in_1(read_real_bit), .out(multiplexer_10_out[3]));
  Multiplexer multiplexer_14 (.sel(read_bit4), .in_0(Read_out[3]), .in_1(read_real_bit), .out(multiplexer_10_out[4]));
  Multiplexer multiplexer_15 (.sel(read_bit5), .in_0(Read_out[4]), .in_1(read_real_bit), .out(multiplexer_10_out[5]));
  Multiplexer multiplexer_16 (.sel(read_bit6), .in_0(Read_out[5]), .in_1(read_real_bit), .out(multiplexer_10_out[6]));
  Multiplexer multiplexer_17 (.sel(read_bit7), .in_0(Read_out[6]), .in_1(read_real_bit), .out(multiplexer_10_out[7]));
  Multiplexer multiplexer_18 (.sel(read_bit8), .in_0(Read_out[7]), .in_1(read_real_bit), .out(multiplexer_10_out[8]));
  Multiplexer multiplexer_19 (
    .sel(read_bit9), .in_0(read_byteout[9]), .in_1(read_real_bit), .out(multiplexer_10_out[9]));
  Register #(.Bits(9)) check_read_reg (.D(read_in), .C(InnerClock), .en(~Read_ready), .Q(read_ret));
  BitCount #(.Bits(9)) bitcount_1 (.in(read_ret), .out(bitcount_1_out));
  assign driver_7_out = bit_9 ? bitcount_1_out : 4'bz;  // Driver driver_7
  Comparator #(.Bits(4)) comparator_3 (.a(driver_7_out), .b(4'b0100), .gt(comparator_3_gt));  // open: eq, lt
  Register #(.Bits(10)) register_1 (
    .D(read_bytein), .C(InnerClock), .en(~Read_ready), .Q({read_byteout[9], Read_out, read_byteout[0]}));
  assign read_bytein = read_en_t ? multiplexer_10_out : 10'bz;  // Driver driver_8
  Register register_2 (.D(comparator_3_gt), .C(InnerClock), .en(bit_9), .Q(read_real_bit));

  // Other names for the same wires on the sheet: C = Clock; check_c = InnerClock; r_begin = read_en; read_bit = RX;
  //   read_byteout[8:1] = Read_out; rs3 = Read_ready; send_bit = TX; w_begin = write_en; ws0 = Writeable

  // Notes on the sheet:
  //   InnerClock: Hz: 20
  //   ws0: wait start
  //   ws1: send bits
  //   ws2: complate
  //   ws3: complate
  //   16 times clock frequency sampling circuit
  //   rs0: wait start
  //   rs1: read bits wait count 9
  //   rs2: wait stop
  //   rs3: wait out read
endmodule
