// Digital circuit vga.dig as structural Verilog
module vga (
  input  clk
);

  wire H, Hori_next, V;
  wire [15:0] Hori_v, Vert_v;

  vga_timing Hori (
    .en(1'b1), .clk(clk), .res(16'h280), .fp(16'h10), .sync(16'h60), .bp(16'h30), .pol(1'b1),
    .next(Hori_next), .pulse_s(H), .V(Hori_v));
  vga_timing Vert (
    .en(Hori_next), .clk(clk), .res(16'h1e0), .fp(16'hb), .sync(16'h2), .bp(16'h21), .pol(1'b1), .pulse_s(V),
    .V(Vert_v));  // open: next
  VGA vga_1 (.R(Hori_v[5:0]), .G(Vert_v[5:0]), .B(Hori_v[11:6]), .H(H), .V(V), .C(clk));

  // Other names for the same wires on the sheet: c = clk

  // Notes on the sheet:
  //   clk: Hz: 2147483647
endmodule
