// Digital circuit vga_timing.dig as structural Verilog
module vga_timing (
  input  en,
  input  clk,
  input  [15:0] res,
  input  [15:0] fp,
  input  [15:0] sync,
  input  [15:0] bp,
  input  pol,
  output next,
  output pulse_s,
  output [15:0] V
);

  wire comparator_1_eq, comparator_2_eq, comparator_3_eq, or_1_out, t_ff_1_q;
  wire [15:0] sub_1_s, sub_2_s, sub_3_s, sub_4_s;

  Sub #(.Bits(16)) sub_1 (.a({16{1'b0}}), .b(bp), .c_i(1'b0), .s(sub_1_s));  // open: c_o
  Sub #(.Bits(16)) sub_2 (.a(res), .b(16'h1), .c_i(1'b0), .s(sub_2_s));  // open: c_o
  Comparator #(.Signed("true"), .Bits(16)) comparator_1 (.a(V), .b(sub_1_s), .eq(comparator_1_eq));  // open: gt, lt
  Sub #(.Bits(16)) sub_3 (.a(sub_1_s), .b(sync), .c_i(1'b0), .s(sub_3_s));  // open: c_o
  Comparator #(.Bits(16)) comparator_2 (.a(V), .b(sub_2_s), .eq(comparator_2_eq));  // open: gt, lt
  and and_1 (next, en, comparator_2_eq);
  Comparator #(.Signed("true"), .Bits(16)) comparator_3 (.a(V), .b(sub_3_s), .eq(comparator_3_eq));  // open: gt, lt
  Sub #(.Bits(16)) sub_4 (.a(sub_3_s), .b(fp), .c_i(1'b0), .s(sub_4_s));  // open: c_o
  or or_1 (or_1_out, comparator_1_eq, comparator_3_eq);
  CounterPreset #(.Bits(16)) counterpreset_1 (
    .en(en), .C(clk), .dir(1'b0), .in(sub_4_s), .ld(next), .clr(1'b0), .out(V));  // open: ovf
  T_FF t_ff_1 (.T(or_1_out), .C(clk), .Q(t_ff_1_q));  // open: nQ
  xor xor_1 (pulse_s, t_ff_1_q, pol);

  // Other names for the same wires on the sheet: c = clk; pixel_cur[15:0] = V

  // Notes on the sheet:
  //   res: resolution, default 5
  //   fp: front portch, default 2
  //   sync: default 3
  //   bp: back portch, default 4
  //   next: switch to next line
  //   pulse_s: sync pulse
  //   pol: polarity of the sync signal (0 for active high)
endmodule
