// Digital circuit which_memory.dig as structural Verilog
module which_memory (
  input  [31:0] mem_addr,
  output Oe_ker,
  output OE_ssd,
  output [23:0] SSD_addr
);

  and and_1 (OE_ssd, mem_addr[30], ~mem_addr[31]);  // And
  and and_2 (Oe_ker, ~mem_addr[30], ~mem_addr[31]);  // And

  assign SSD_addr = mem_addr[23:0];
endmodule
