// Digital circuit main.dig as structural Verilog
module main (
  input  Clock,
  input  TimerClock,
  input  GPIO_in1,
  input  GPIO_in2,
  input  GPIO_in3,
  input  GPIO_in4,
  input  GPIO_in5,
  input  GPIO_in6,
  input  GPIO_in7,
  input  GPIO_in8,
  input  GPIO_in9,
  input  GPIO_in10,
  output GPIO_1,
  output GPIO_2,
  output GPIO_3,
  output GPIO_4,
  output GPIO_5,
  output GPIO_6,
  output GPIO_7,
  output GPIO_8,
  output GPIO_9,
  output GPIO_10
);

  wire and_1_out, and_2_out, ard_en, crd_en, cust_ctrl_1_pc_init, Cust_op, int_peripheral, jrd_en, lrd_en,
       mechine_op_unit_1_mret, memgpio_en, or_1_out, or_2_out, PC_except, PC_jmp, plic_1_gate_peripheral,
       plic_1_mip_seten, plic_1_out_en, We_mem, which_memory_1_oe_ker, which_memory_1_oe_ssd;
  wire [3:0] storebytes_size;
  wire [4:0] driver_9_out, instruction_decoder_1_rs1, instruction_decoder_1_rs2, rd;
  wire [5:0] instruction_decoder_1_csr_op;
  wire [6:0] imm_7;
  wire [7:0] instruction_decoder_1_mechie_op, rom_1_d;
  wire [8:0] instruction_decoder_1_jmp_op, instruction_decoder_1_mem_op;
  wire [11:0] csr_1_addr_csr, imm_12;
  wire [18:0] instruction_decoder_1_alu_op;
  wire [19:0] imm_20;
  wire [23:0] which_memory_1_ssd_addr;
  wire [31:0] Addr_except, Addr_jmp, alu_1_rd_out, csr_1_out_csr, csr_1_rd_out, data_mem, data_memgpio,
       data_memrdin, debug_data, debug_info, driver_1_out, driver_3_out, driver_5_out, instruction_code,
       instuction_jump_unit_1_rd_out, int_bus_1_int_code, int_except_unit_1_mip_out, int_gpiocode,
       int_iiccode, int_uartcode, Invalid_op, mem_addr, memory_1_data_out, memory_operation_unit_1_rd_out,
       Out_csr1, PC_exec, PC_next, plic_1_mip_set, plic_1_out_ra, rs1_data, rs2_data;

  PullDown pulldown_1 (.out(PC_except));
  and and_1 (and_1_out, PC_jmp, ~PC_except);  // And
  or or_1 (or_1_out, PC_jmp, PC_except);
  assign driver_1_out = and_1_out ? Addr_jmp : 32'bz;  // Driver driver_1
  assign driver_1_out = PC_except ? Addr_except : 32'bz;  // Driver driver_2
  cust_ctrl cust_ctrl_1 (.op_code(instruction_code), .cust_code(Cust_op), .Clock(Clock), .PC_init(cust_ctrl_1_pc_init));
  program_counter program_counter_1 (
    .PC_inited(cust_ctrl_1_pc_init), .En(1'b1), .Clock(Clock), .Addr_jmp(driver_1_out), .En_jmp(or_1_out),
    .PC_next(PC_next), .PC_exec(PC_exec));
  gpio u_gpio_1 (
    .Clock(Clock), .Addr_w(mem_addr), .Data_in(data_mem), .we(We_mem), .Addr_rd(mem_addr),
    .int_gate(int_peripheral), .GPIO1_in(GPIO_in1), .GPIO2_in(GPIO_in2), .GPIO3_in(GPIO_in3),
    .GPIO4_in(GPIO_in4), .GPIO5_in(GPIO_in5), .GPIO6_in(GPIO_in6), .GPIO7_in(GPIO_in7), .GPIO8_in(GPIO_in8),
    .GPIO9_in(GPIO_in9), .GPIO10_in(GPIO_in10), .Out_rd(data_memgpio), .Out_en(memgpio_en),
    .perint_code(int_gpiocode), .GPIO1_out(GPIO_1), .GPIO2_out(GPIO_2), .GPIO3_out(GPIO_3),
    .GPIO4_out(GPIO_4), .GPIO5_out(GPIO_5), .GPIO6_out(GPIO_6), .GPIO7_out(GPIO_7), .GPIO8_out(GPIO_8),
    .GPIO9_out(GPIO_9), .GPIO10_out(GPIO_10));
  which_memory which_memory_1 (
    .mem_addr(mem_addr), .Oe_ker(which_memory_1_oe_ker), .OE_ssd(which_memory_1_oe_ssd),
    .SSD_addr(which_memory_1_ssd_addr));
  and and_2 (and_2_out, PC_exec[25], ~PC_exec[31]);  // And
  memory memory_1 (
    .OE_PC(and_2_out), .Addr_PC(PC_exec), .WE(We_mem), .Addr(mem_addr), .Data_in(data_mem),
    .ByteSize_in(storebytes_size), .Clock(Clock), .DataPC_out(instruction_code), .Data_out(memory_1_data_out));
  ROM #(.AddrBits(24), .Bits(8)) rom_1 (.A(which_memory_1_ssd_addr), .sel(1'b1), .D(rom_1_d));
  boot_rom boot_rom_1 (.Addr(PC_exec[23:0]), .En(PC_exec[31]), .Out_code(instruction_code));
  assign driver_3_out = which_memory_1_oe_ker ? memory_1_data_out : 32'bz;  // Driver driver_3
  assign driver_3_out = which_memory_1_oe_ssd ? {{24{1'b0}}, rom_1_d} : 32'bz;  // Driver driver_4
  instruction_decoder instruction_decoder_1 (
    .Instruction_In(instruction_code), .EN(1'b1), .rd(rd), .rs1(instruction_decoder_1_rs1),
    .rs2(instruction_decoder_1_rs2), .imm_2531(imm_7), .imm_1231(imm_20), .imm_2032(imm_12),
    .invalid(Invalid_op), .csr_op(instruction_decoder_1_csr_op), .jmp_op(instruction_decoder_1_jmp_op),
    .alu_op(instruction_decoder_1_alu_op), .mem_op(instruction_decoder_1_mem_op),
    .mechie_op(instruction_decoder_1_mechie_op), .cust_op(Cust_op));
  csr csr_1 (
    .CSRCode_in(instruction_decoder_1_csr_op), .Data_in(rs1_data), .Csr_Addr(imm_12),
    .Imm5_in(instruction_decoder_1_rs1), .Data_temp(Out_csr1), .Clock(Clock), .En(crd_en),
    .rd_out(csr_1_rd_out), .Out_csr(csr_1_out_csr), .Addr_csr(csr_1_addr_csr));
  PullDown #(.Bits(32)) pulldown_2 (.out(Out_csr1));
  mechine_op_unit mechine_op_unit_1 (.mechine_op(instruction_decoder_1_mechie_op), .mret(mechine_op_unit_1_mret));
  alu alu_1 (
    .Alu_in(instruction_decoder_1_alu_op), .rs1_in(rs1_data), .rs2_in(rs2_data), .Imm12_in(imm_12),
    .EN_out(ard_en), .rd_out(alu_1_rd_out), .InvalidOP_out(Invalid_op));
  memory_operation_unit memory_operation_unit_1 (
    .MemOp_in(instruction_decoder_1_mem_op), .Data_in(driver_3_out), .rs1(rs1_data), .rs2(rs2_data),
    .Offset_12(imm_12), .Offset_7(imm_7), .Offset_5(rd), .imm_20(imm_20), .rEN_out(lrd_en),
    .rd_out(memory_operation_unit_1_rd_out), .mwe_out(We_mem), .Addr_out(mem_addr), .Mem_out(data_mem),
    .StoreByteSize_out(storebytes_size));
  instuction_jump_unit instuction_jump_unit_1 (
    .jmp_op(instruction_decoder_1_jmp_op), .PC_cur(PC_exec), .rs1_in(rs1_data), .rs2_in(rs2_data),
    .Imm12_in(imm_12), .Imm20_in(imm_20), .Imm7_in(imm_7), .offset_5(rd), .EN_out(jrd_en),
    .rd_out(instuction_jump_unit_1_rd_out), .Addr_jmp(Addr_jmp), .En_jmp(PC_jmp));
  or or_2 (or_2_out, crd_en, jrd_en, ard_en, lrd_en);
  assign driver_5_out = crd_en ? csr_1_rd_out : 32'bz;  // Driver driver_5
  assign driver_5_out = jrd_en ? instuction_jump_unit_1_rd_out : 32'bz;  // Driver driver_6
  assign driver_5_out = ard_en ? alu_1_rd_out : 32'bz;  // Driver driver_7
  assign driver_5_out = lrd_en ? memory_operation_unit_1_rd_out : 32'bz;  // Driver driver_8
  assign driver_9_out = or_2_out ? rd : 5'bz;  // Driver driver_9
  PullDown #(.Bits(5)) pulldown_3 (.out(driver_9_out));
  reg_file_riscv reg_file_riscv_1 (
    .WE(driver_9_out), .OE_P1(instruction_decoder_1_rs1), .OE_P2(instruction_decoder_1_rs2),
    .OE_P3(5'b01110), .Din(driver_5_out), .Clock(Clock), .Output_P1(rs1_data), .Output_P2(rs2_data),
    .Output_P3(debug_data));
  PLIC plic_1 (
    .WE(We_mem), .perint_code(int_bus_1_int_code), .Addr_w(mem_addr), .Addr_r1(mem_addr), .Data_in(data_mem),
    .mip_in(int_except_unit_1_mip_out), .mret(mechine_op_unit_1_mret), .TimerClock(TimerClock),
    .Clock(Clock), .mip_seten(plic_1_mip_seten), .mip_set(plic_1_mip_set), .Out_en(plic_1_out_en),
    .Out_ra(plic_1_out_ra), .gate_peripheral(plic_1_gate_peripheral));  // open: int_timer, mtimcmp, mtime
  int_except_unit int_except_unit_1 (
    .WE_CSR(crd_en), .Data_csr(csr_1_out_csr), .Addr_csrw(csr_1_addr_csr), .Addr_csr1(csr_1_addr_csr),
    .Addr_csr2({12{1'b0}}), .Exception_code(Invalid_op), .PC_Addr(PC_exec), .PC_ip(instruction_code),
    .PC_next(PC_next), .mret(mechine_op_unit_1_mret), .mip_en(plic_1_mip_seten), .mip_in(plic_1_mip_set),
    .Clock(Clock), .Out_csr1(Out_csr1), .En_jmp(PC_except), .Addr_jmp(Addr_except),
    .mip_out(int_except_unit_1_mip_out), .mepc_out(debug_info));  // open: Out_csr2, mie_out, ecode_out, timer_en
  assign data_memrdin = plic_1_out_en ? plic_1_out_ra : 32'bz;  // Driver driver_10
  int_bus int_bus_1 (
    .int_gate(plic_1_gate_peripheral), .int_uart(int_uartcode), .int_gpio(int_gpiocode),
    .int_iic(int_iiccode), .Clock(Clock), .int_gateout(int_peripheral), .int_code(int_bus_1_int_code));

  // Other names for the same wires on the sheet: c = Clock; gpio_out1 = GPIO_1; gpio_out2 = GPIO_2;
  //   gpio_out3 = GPIO_3; gpio_out4 = GPIO_4; gpio_out5 = GPIO_5; gpio_out6 = GPIO_6; gpio_out7 = GPIO_7;
  //   gpio_out8 = GPIO_8; gpio_out9 = GPIO_9; gpio_out10 = GPIO_10

  // Notes on the sheet:
  //   Clock: Hz: 50000
  //   TimerClock: Hz: 100
  //   Peripheral GPIO
  //   contents of rom_1 (hex, n*v repeats v):
  //   97,7,0,0,93,87,47,2,93,87,17,0,f3,93,57,30,37,2e,0,0,13,e,8e,80
  //   ,f3,13,e,30,37,1,0,1,ef,0,90,32,ef,0,40,9,73,0,20,30,13,0,0,0
  //   ,13,0,0,0,13,0,0,0,13,0,0,0,13,0,0,0,ef,0,0,54,73,0,20,30,13,0,0,0
  //   ,13,0,0,0,ef,0,80,1,ef,0,0,54,ef,0,0,3,73,0,20,30,f3,13,45,30
  //   ,67,80,0,0,13,1,81,fe,23,20,c1,0,23,22,d1,0,23,24,e1,0,23,26,f1
  //   ,0,23,28,1,1,23,2a,11,1,67,80,0,0,3,26,1,0,83,26,41,0,3,27,81
  //   ,0,83,27,c1,0,3,28,1,1,83,28,41,1,13,1,81,1,67,80,0,0,ef,f0,1f
  //   ,fc,ef,0,40,4d,ef,f0,9f,fd,67,80,0,0,ef,f0,1f,fb,ef,0,0,4c,ef
  //   ,f0,9f,fc,73,0,20,30,67,80,0,0,13,1,1,ff,13,5,f0,7,23,26,11,0
  //   ,ef,0,c0,3b,b7,17,0,2,83,a7,87,c4,63,86,7,6,23,24,81,0,37,14,0
  //   ,2,83,27,4,c4,63,92,7,4,ef,0,40,3f,13,65,f5,7,ef,0,0,3e,93,7,10
  //   ,0,23,20,f4,c4,3,24,81,0,37,15,0,2,13,5,45,b5,ef,0,0,5e,83,20
  //   ,c1,0,37,6,0,2,13,6,c6,c,13,5,40,1f,93,5,0,0,13,1,1,1,6f,0,90
  //   ,10,ef,0,40,3b,13,75,5,f8,ef,0,0,3a,23,20,4,c4,3,24,81,0,6f,f0
  //   ,5f,fc,ef,0,c0,39,13,75,5,f8,ef,0,80,38,b7,17,0,2,3,a5,47,c4,13
  //   ,7,70,0,13,5,15,0,63,4c,a7,0,13,7,5,0,93,5,10,0,23,a2,e7,c4,ef
  //   ,0,40,32,6f,f0,1f,f9,13,7,10,0,13,5,7,0,6f,f0,9f,fe,13,1,1,ff
  //   ,13,5,a0,0,23,26,11,0,ef,0,c0,35,b7,17,0,2,23,a4,a7,c4,ef,0,c0
  //   ,36,83,20,c1,0,37,15,0,2,13,5,85,b6,13,1,1,1,6f,0,c0,53,13,1,1
  //   ,ff,13,5,f0,7,23,22,91,0,23,20,21,1,23,26,11,0,23,24,81,0,b7,14
  //   ,0,2,ef,0,80,2b,13,9,80,0,13,5,a0,0,ef,0,0,31,23,a4,a4,c4,13,4
  //   ,10,0,63,4,5,4,ef,0,40,2f,13,65,f5,7,ef,0,0,2e,93,5,0,0,13,5,40
  //   ,1f,ef,0,d0,e,ef,0,c0,2d,13,75,5,f8,ef,0,80,2c,13,5,40,1f,93,5
  //   ,0,0,ef,0,50,d,13,5,a0,0,ef,0,c0,2c,23,a4,a4,c4,13,4,10,0,e3,10
  //   ,5,fc,13,5,4,0,93,5,10,0,ef,0,c0,25,13,5,40,1f,93,5,0,0,ef,0,90
  //   ,a,13,5,4,0,93,5,0,0,13,4,14,0,ef,0,0,24,e3,0,24,f9,83,a7,84,c4
  //   ,e3,88,7,fc,6f,f0,5f,f7,13,1,1,ff,23,26,11,0,ef,0,d0,2,37,6,0
  //   ,2,93,5,0,0,13,6,c6,c,13,5,40,1f,ef,0,c0,7a,b7,5,0,2,93,85,5,19
  //   ,13,5,10,0,ef,0,0,28,6f,0,0,0,13,1,1,fc,23,2e,11,2,23,28,21,3
  //   ,23,26,31,3,23,22,51,3,23,20,61,3,23,2e,71,1,23,2c,81,1,23,2a
  //   ,91,1,23,2c,81,2,23,2a,91,2,23,24,41,3,ef,0,40,2f,13,6,10,0,93
  //   ,5,6,0,13,5,6,0,ef,0,40,52,13,6,40,6,93,5,20,0,13,5,10,0,ef,0
  //   ,40,51,93,9,f1,0,37,1b,0,2,b7,1a,0,2,b7,1c,0,2,37,1c,0,2,b7,1b
  //   ,0,2,13,9,a0,0,93,5,0,0,13,5,10,0,ef,0,0,5b,13,a,5,0,13,5,b,b8
  //   ,ef,0,c0,3c,93,4,c1,0,23,26,1,0,ef,0,80,3f,13,4,5,0,63,a,25,1
  //   ,ef,0,80,2e,93,84,14,0,a3,8f,84,fe,e3,94,34,ff,13,85,8a,ba,ef
  //   ,0,0,3a,13,5,c1,0,ef,0,c0,5,63,0,aa,2,63,78,aa,0,13,5,8c,bb,ef
  //   ,0,80,38,6f,f0,5f,fb,13,85,4b,bc,ef,0,c0,37,6f,f0,9f,fa,13,85
  //   ,cc,ba,ef,0,0,37,6f,f0,df,f8,13,1,1,ff,23,24,81,0,23,26,11,0,13
  //   ,4,5,0,63,4,6,0,ef,f0,df,fe,83,20,c1,0,13,5,4,0,3,24,81,0,13,1,1,1
  //   ,67,80,0,0,3,47,5,0,93,7,5,0,13,5,0,0,63,6,7,2,93,87,17,0,13,16
  //   ,25,0,93,6,7,fd,33,5,c5,0,3,c7,7,0,13,15,15,0,33,5,d5,0,13,75
  //   ,f5,f,e3,10,7,fe,67,80,0,0,67,80,0,0,b7,17,0,2,93,87,7,bd,83,a6
  //   ,47,0,3,d7,87,0,3,a6,7,0,83,c7,a7,0,13,1,1,ff,23,24,d1,0,23,16
  //   ,e1,0,a3,81,5,0,23,22,c1,0,23,7,f1,0,13,7,90,0,93,86,25,0,63,56
  //   ,a7,2,93,7,5,0,13,5,0,0,93,87,67,ff,13,5,15,0,e3,4c,f7,fe,b3,87
  //   ,27,0,83,c7,47,0,93,86,f6,ff,a3,80,f6,0,e3,4e,a7,fc,33,5,25,0
  //   ,83,47,45,0,13,85,5,0,23,80,f6,0,13,1,1,1,67,80,0,0,63,8e,5,0
  //   ,b7,7,0,a0,3,a7,7,0,13,5,f5,ff,b3,95,a5,0,b3,e5,e5,0,23,a0,b7
  //   ,0,67,80,0,0,b7,7,0,a0,23,a0,a7,0,67,80,0,0,37,7,0,a0,13,5,f5
  //   ,ff,93,7,10,0,13,7,47,0,3,27,7,0,b3,97,a7,0,63,8a,5,0,33,67,f7
  //   ,0,b7,7,0,a0,23,a2,e7,0,67,80,0,0,93,c7,f7,ff,33,f7,e7,0,b7,7
  //   ,0,a0,23,a2,e7,0,67,80,0,0,b7,7,0,a0,23,a2,a7,0,67,80,0,0,b7,7
  //   ,0,a0,3,a5,47,0,67,80,0,0,b7,7,0,a0,83,a6,47,0,13,7,f5,ff,93,7
  //   ,10,0,b3,97,e7,0,33,f5,d7,0,67,80,0,0,b7,7,0,a0,23,a4,7,0,67,80
  //   ,0,0,b7,17,0,2,b7,16,0,2,13,15,25,0,93,87,c7,bd,3,a7,c6,c4,b3
  //   ,87,a7,0,23,a0,b7,0,93,7,f0,7f,63,f4,e7,0,67,80,0,0,b7,17,0,0
  //   ,93,87,7,80,33,65,f7,0,23,a6,a6,c4,6f,f0,9f,b0,37,17,0,2,83,27
  //   ,c7,c4,13,6,5,0,b7,16,0,2,13,e5,7,8,23,a8,c6,c4,23,26,a7,c4,6f
  //   ,f0,9f,ae,67,80,0,0,b7,17,0,2,83,a7,7,c5,63,84,7,0,67,80,7,0,67
  //   ,80,0,0,b7,17,0,b0,3,a7,7,0,b7,17,0,2,93,87,c7,bd,13,17,27,0,b3
  //   ,87,e7,0,83,a7,7,0,63,84,7,0,67,80,7,0,67,80,0,0,b7,17,0,2,13
  //   ,7,10,0,23,aa,e7,c4,67,80,0,0,13,1,1,ff,23,24,81,0,37,14,0,2,83
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endmodule
